// Logisim project CPU Proto1.circ as structural Verilog
module MEM_1 (
  input  s,
  input  E,
  output Q
);

  wire nand_1_out, nand_2_out, nand_4_out;

  nand nand_1 (nand_1_out, s, E);
  nand nand_2 (nand_2_out, nand_1_out, E);
  nand nand_3 (Q, nand_1_out, nand_4_out);
  nand nand_4 (nand_4_out, Q, nand_2_out);
endmodule

module MEM_8 (
  input  [7:0] \input ,
  input  set,
  output [7:0] out_3
);

  MEM_1 mem_1_1 (.s(\input [0]), .E(set), .Q(out_3[0]));
  MEM_1 mem_1_2 (.s(\input [1]), .E(set), .Q(out_3[1]));
  MEM_1 mem_1_3 (.s(\input [2]), .E(set), .Q(out_3[2]));
  MEM_1 mem_1_4 (.s(\input [3]), .E(set), .Q(out_3[3]));
  MEM_1 mem_1_5 (.s(\input [4]), .E(set), .Q(out_3[4]));
  MEM_1 mem_1_6 (.s(\input [5]), .E(set), .Q(out_3[5]));
  MEM_1 mem_1_7 (.s(\input [6]), .E(set), .Q(out_3[6]));
  MEM_1 mem_1_8 (.s(\input [7]), .E(set), .Q(out_3[7]));
endmodule

module CPU_ENABLE (
  input  [7:0] \input ,
  input  enable,
  output [7:0] out_3
);

  and and_1 (out_3[0], \input [0], enable);
  and and_2 (out_3[1], \input [1], enable);
  and and_3 (out_3[2], \input [2], enable);
  and and_4 (out_3[3], \input [3], enable);
  and and_5 (out_3[4], \input [4], enable);
  and and_6 (out_3[5], \input [5], enable);
  and and_7 (out_3[6], \input [6], enable);
  and and_8 (out_3[7], \input [7], enable);
endmodule

module DECODER_3x8 (
  input  MSB,
  input  middle,
  input  LSB,
  output [7:0] out_4
);

  wire not_1_out, not_2_out, not_3_out;

  not not_1 (not_1_out, MSB);
  not not_2 (not_2_out, middle);
  not not_3 (not_3_out, LSB);
  and _000 (out_4[0], not_1_out, not_2_out, not_3_out);
  and _001 (out_4[1], not_1_out, not_2_out, LSB);
  and _010 (out_4[2], not_1_out, middle, not_3_out);
  and _011 (out_4[3], not_1_out, middle, LSB);
  and _100 (out_4[4], MSB, not_2_out, not_3_out);
  and _101 (out_4[5], MSB, not_2_out, LSB);
  and _110 (out_4[6], MSB, middle, not_3_out);
  and _111 (out_4[7], MSB, middle, LSB);
endmodule

module DECODER_4x16 (
  input  [3:0] \input ,
  output LSB,
  output out_3,
  output out_4,
  output out_5,
  output out_6,
  output out_7,
  output out_8,
  output out_9,
  output out_10,
  output out_11,
  output out_12,
  output out_13,
  output out_14,
  output out_15,
  output out_16,
  output MSB
);

  wire not_1_out, not_2_out, not_3_out, not_4_out;

  not not_1 (not_1_out, \input [0]);
  not not_2 (not_2_out, \input [1]);
  not not_3 (not_3_out, \input [2]);
  not not_4 (not_4_out, \input [3]);
  and _0000 (LSB, not_4_out, not_3_out, not_2_out, not_1_out);
  and _0001 (out_3, not_4_out, not_3_out, not_2_out, \input [0]);
  and _0010 (out_4, not_4_out, not_3_out, \input [1], not_1_out);
  and _0011 (out_5, not_4_out, not_3_out, \input [1], \input [0]);
  and _0100 (out_6, not_4_out, \input [2], not_2_out, not_1_out);
  and _0101 (out_7, not_4_out, \input [2], not_2_out, \input [0]);
  and _0110 (out_8, not_4_out, \input [2], \input [1], not_1_out);
  and _0111 (out_9, not_4_out, \input [2], \input [1], \input [0]);
  and _1000 (out_10, \input [3], not_3_out, not_2_out, not_1_out);
  and _1001 (out_11, \input [3], not_3_out, not_2_out, \input [0]);
  and _1010 (out_12, \input [3], not_3_out, \input [1], not_1_out);
  and _1011 (out_13, \input [3], not_3_out, \input [1], \input [0]);
  and _1100 (out_14, \input [3], \input [2], not_2_out, not_1_out);
  and _1101 (out_15, \input [3], \input [2], not_2_out, \input [0]);
  and _1110 (out_16, \input [3], \input [2], \input [1], not_1_out);
  and _1111 (MSB, \input [3], \input [2], \input [1], \input [0]);
endmodule

module REGISTER (
  input  [7:0] input__write__data,
  input  set_bit,
  input  enable,
  output [7:0] current_register_data,
  output [7:0] output__read__bits
);

  wire [7:0] cpu_enable_1_out_3;

  MEM_8 mem_8_1 (.\input (input__write__data), .out_3(current_register_data), .set(set_bit));
  CPU_ENABLE cpu_enable_1 (.\input (current_register_data), .out_3(cpu_enable_1_out_3), .enable(enable));
  assign output__read__bits = enable ? cpu_enable_1_out_3 : 8'bz;  // Controlled_Buffer controlled_buffer_1

  // Notes on the sheet:
  //   designed for RAM memory matrix 
  //   built in buffer
endmodule

module BYTE_REGISTER (
  input  row__n,
  input  [7:0] \input ,
  input  col__m,
  input  reset,
  input  set__write_mode,
  input  enable__read_mode,
  output [7:0] contents,
  output [7:0] \output 
);

  wire Active, read_out, reset_out, write_out;
  wire [7:0] register_1_output__read__bits;

  and entry (Active, row__n, col__m);
  and write (write_out, Active, set__write_mode);
  and read (read_out, enable__read_mode, Active);
  or u_reset (reset_out, reset, write_out);
  REGISTER register_1 (
    .input__write__data(\input ), .enable(read_out), .current_register_data(contents),
    .output__read__bits(register_1_output__read__bits), .set_bit(reset_out));
  assign \output  = read_out ? register_1_output__read__bits : 8'bz;  // Controlled_Buffer controlled_buffer_1
endmodule

module RANDOM_ACCESS_MEMORY (
  input  [7:0] \input ,
  input  [7:0] desired_address,
  input  set,
  input  enable,
  input  save,
  input  reset,
  output [7:0] \output ,
  output [7:0] out_8,
  output [7:0] out_9,
  output [7:0] out_10,
  output [7:0] out_11,
  output [7:0] out_12,
  output [7:0] out_13,
  output [7:0] out_14,
  output [7:0] out_15,
  output [7:0] out_16,
  output [7:0] out_17,
  output [7:0] out_18,
  output [7:0] out_19,
  output [7:0] out_20,
  output [7:0] out_21,
  output [7:0] out_22,
  output [7:0] out_23,
  output [7:0] out_24,
  output [7:0] out_25,
  output [7:0] out_26,
  output [7:0] out_27,
  output [7:0] out_28,
  output [7:0] out_29,
  output [7:0] out_30,
  output [7:0] out_31,
  output [7:0] out_32,
  output [7:0] out_33,
  output [7:0] out_34,
  output [7:0] out_35,
  output [7:0] out_36,
  output [7:0] out_37,
  output [7:0] out_38,
  output [7:0] out_39,
  output [7:0] out_40,
  output [7:0] out_41,
  output [7:0] out_42,
  output [7:0] out_43,
  output [7:0] out_44,
  output [7:0] out_45,
  output [7:0] out_46,
  output [7:0] out_47,
  output [7:0] out_48,
  output [7:0] out_49,
  output [7:0] out_50,
  output [7:0] out_51,
  output [7:0] out_52,
  output [7:0] out_53,
  output [7:0] out_54,
  output [7:0] out_55,
  output [7:0] out_56,
  output [7:0] out_57,
  output [7:0] out_58,
  output [7:0] out_59,
  output [7:0] out_60,
  output [7:0] out_61,
  output [7:0] out_62,
  output [7:0] out_63,
  output [7:0] out_64,
  output [7:0] out_65,
  output [7:0] out_66,
  output [7:0] out_67,
  output [7:0] out_68,
  output [7:0] out_69,
  output [7:0] out_70,
  output [7:0] out_71,
  output [7:0] out_72,
  output [7:0] out_73,
  output [7:0] out_74,
  output [7:0] out_75,
  output [7:0] out_76,
  output [7:0] out_77,
  output [7:0] out_78,
  output [7:0] out_79,
  output [7:0] out_80,
  output [7:0] out_81,
  output [7:0] out_82,
  output [7:0] out_83,
  output [7:0] out_84,
  output [7:0] out_85,
  output [7:0] out_86,
  output [7:0] out_87,
  output [7:0] out_88,
  output [7:0] out_89,
  output [7:0] out_90,
  output [7:0] out_91,
  output [7:0] out_92,
  output [7:0] out_93,
  output [7:0] out_94,
  output [7:0] out_95,
  output [7:0] out_96,
  output [7:0] out_97,
  output [7:0] out_98,
  output [7:0] out_99,
  output [7:0] out_100,
  output [7:0] out_101,
  output [7:0] out_102,
  output [7:0] out_103,
  output [7:0] out_104,
  output [7:0] out_105,
  output [7:0] out_106,
  output [7:0] out_107,
  output [7:0] out_108,
  output [7:0] out_109,
  output [7:0] out_110,
  output [7:0] out_111,
  output [7:0] out_112,
  output [7:0] out_113,
  output [7:0] out_114,
  output [7:0] out_115,
  output [7:0] out_116,
  output [7:0] out_117,
  output [7:0] out_118,
  output [7:0] out_119,
  output [7:0] out_120,
  output [7:0] out_121,
  output [7:0] out_122,
  output [7:0] out_123,
  output [7:0] out_124,
  output [7:0] out_125,
  output [7:0] out_126,
  output [7:0] out_127,
  output [7:0] out_128,
  output [7:0] out_129,
  output [7:0] out_130,
  output [7:0] out_131,
  output [7:0] out_132,
  output [7:0] out_133,
  output [7:0] out_134,
  output [7:0] out_135,
  output [7:0] out_136,
  output [7:0] out_137,
  output [7:0] out_138,
  output [7:0] out_139,
  output [7:0] out_140,
  output [7:0] out_141,
  output [7:0] out_142,
  output [7:0] out_143,
  output [7:0] out_144,
  output [7:0] out_145,
  output [7:0] out_146,
  output [7:0] out_147,
  output [7:0] out_148,
  output [7:0] out_149,
  output [7:0] out_150,
  output [7:0] out_151,
  output [7:0] out_152,
  output [7:0] out_153,
  output [7:0] out_154,
  output [7:0] out_155,
  output [7:0] out_156,
  output [7:0] out_157,
  output [7:0] out_158,
  output [7:0] out_159,
  output [7:0] out_160,
  output [7:0] out_161,
  output [7:0] out_162,
  output [7:0] out_163,
  output [7:0] out_164,
  output [7:0] out_165,
  output [7:0] out_166,
  output [7:0] out_167,
  output [7:0] out_168,
  output [7:0] out_169,
  output [7:0] out_170,
  output [7:0] out_171,
  output [7:0] out_172,
  output [7:0] out_173,
  output [7:0] out_174,
  output [7:0] out_175,
  output [7:0] out_176,
  output [7:0] out_177,
  output [7:0] out_178,
  output [7:0] out_179,
  output [7:0] out_180,
  output [7:0] out_181,
  output [7:0] out_182,
  output [7:0] out_183,
  output [7:0] out_184,
  output [7:0] out_185,
  output [7:0] out_186,
  output [7:0] out_187,
  output [7:0] out_188,
  output [7:0] out_189,
  output [7:0] out_190,
  output [7:0] out_191,
  output [7:0] out_192,
  output [7:0] out_193,
  output [7:0] out_194,
  output [7:0] out_195,
  output [7:0] out_196,
  output [7:0] out_197,
  output [7:0] out_198,
  output [7:0] out_199,
  output [7:0] out_200,
  output [7:0] out_201,
  output [7:0] out_202,
  output [7:0] out_203,
  output [7:0] out_204,
  output [7:0] out_205,
  output [7:0] out_206,
  output [7:0] out_207,
  output [7:0] out_208,
  output [7:0] out_209,
  output [7:0] out_210,
  output [7:0] out_211,
  output [7:0] out_212,
  output [7:0] out_213,
  output [7:0] out_214,
  output [7:0] out_215,
  output [7:0] out_216,
  output [7:0] out_217,
  output [7:0] out_218,
  output [7:0] out_219,
  output [7:0] out_220,
  output [7:0] out_221,
  output [7:0] out_222,
  output [7:0] out_223,
  output [7:0] out_224,
  output [7:0] out_225,
  output [7:0] out_226,
  output [7:0] out_227,
  output [7:0] out_228,
  output [7:0] out_229,
  output [7:0] out_230,
  output [7:0] out_231,
  output [7:0] out_232,
  output [7:0] out_233,
  output [7:0] out_234,
  output [7:0] out_235,
  output [7:0] out_236,
  output [7:0] out_237,
  output [7:0] out_238,
  output [7:0] out_239,
  output [7:0] out_240,
  output [7:0] out_241,
  output [7:0] out_242,
  output [7:0] out_243,
  output [7:0] out_244,
  output [7:0] out_245,
  output [7:0] out_246,
  output [7:0] out_247,
  output [7:0] out_248,
  output [7:0] out_249,
  output [7:0] out_250,
  output [7:0] out_251,
  output [7:0] out_252,
  output [7:0] out_253,
  output [7:0] out_254,
  output [7:0] out_255,
  output [7:0] out_256,
  output [7:0] out_257,
  output [7:0] out_258,
  output [7:0] out_259,
  output [7:0] out_260,
  output [7:0] out_261,
  output [7:0] out_262,
  output [7:0] out_263
);

  wire byte_register_110_p3, decoder_4x16_1_lsb, decoder_4x16_1_msb, decoder_4x16_1_out_3,
       decoder_4x16_1_out_4, decoder_4x16_1_out_5, decoder_4x16_1_out_6, decoder_4x16_1_out_7,
       decoder_4x16_1_out_8, decoder_4x16_1_out_9, decoder_4x16_1_out_10, decoder_4x16_1_out_11,
       decoder_4x16_1_out_12, decoder_4x16_1_out_13, decoder_4x16_1_out_14, decoder_4x16_1_out_15,
       decoder_4x16_1_out_16, decoder_4x16_2_lsb, decoder_4x16_2_msb, decoder_4x16_2_out_3,
       decoder_4x16_2_out_4, decoder_4x16_2_out_5, decoder_4x16_2_out_6, decoder_4x16_2_out_7,
       decoder_4x16_2_out_8, decoder_4x16_2_out_9, decoder_4x16_2_out_10, decoder_4x16_2_out_12,
       decoder_4x16_2_out_13, decoder_4x16_2_out_14, decoder_4x16_2_out_15, decoder_4x16_2_out_16;
  wire [7:0] mem_8_1_out_3, o;

  MEM_8 mem_8_1 (.\input (desired_address), .out_3(mem_8_1_out_3), .set(save));
  DECODER_4x16 decoder_4x16_1 (
    .\input (mem_8_1_out_3[7:4]), .LSB(decoder_4x16_1_lsb), .out_3(decoder_4x16_1_out_3),
    .out_4(decoder_4x16_1_out_4), .out_5(decoder_4x16_1_out_5), .out_6(decoder_4x16_1_out_6),
    .out_7(decoder_4x16_1_out_7), .out_8(decoder_4x16_1_out_8), .out_9(decoder_4x16_1_out_9),
    .out_10(decoder_4x16_1_out_10), .out_11(decoder_4x16_1_out_11), .out_12(decoder_4x16_1_out_12),
    .out_13(decoder_4x16_1_out_13), .out_14(decoder_4x16_1_out_14), .out_15(decoder_4x16_1_out_15),
    .out_16(decoder_4x16_1_out_16), .MSB(decoder_4x16_1_msb));
  assign \output  = enable ? o : 8'bz;  // Controlled_Buffer controlled_buffer_1
  BYTE_REGISTER byte_register_1 (
    .contents(out_8), .row__n(decoder_4x16_1_lsb), .\input (\input ), .col__m(decoder_4x16_2_msb),
    .reset(reset), .set__write_mode(set), .enable__read_mode(enable), .\output (o));
  BYTE_REGISTER byte_register_2 (
    .contents(out_24), .row__n(decoder_4x16_1_out_3), .\input (\input ), .col__m(decoder_4x16_2_msb),
    .reset(reset), .set__write_mode(set), .enable__read_mode(enable), .\output (o));
  BYTE_REGISTER byte_register_3 (
    .contents(out_40), .row__n(decoder_4x16_1_out_4), .\input (\input ), .col__m(decoder_4x16_2_msb),
    .reset(reset), .set__write_mode(set), .enable__read_mode(enable), .\output (o));
  BYTE_REGISTER byte_register_4 (
    .contents(out_56), .row__n(decoder_4x16_1_out_5), .\input (\input ), .col__m(decoder_4x16_2_msb),
    .reset(reset), .set__write_mode(set), .enable__read_mode(enable), .\output (o));
  BYTE_REGISTER byte_register_5 (
    .contents(out_72), .row__n(decoder_4x16_1_out_6), .\input (\input ), .col__m(decoder_4x16_2_msb),
    .reset(reset), .set__write_mode(set), .enable__read_mode(enable), .\output (o));
  BYTE_REGISTER byte_register_6 (
    .contents(out_88), .row__n(decoder_4x16_1_out_7), .\input (\input ), .col__m(decoder_4x16_2_msb),
    .reset(reset), .set__write_mode(set), .enable__read_mode(enable), .\output (o));
  BYTE_REGISTER byte_register_7 (
    .contents(out_104), .row__n(decoder_4x16_1_out_8), .\input (\input ), .col__m(decoder_4x16_2_msb),
    .reset(reset), .set__write_mode(set), .enable__read_mode(enable), .\output (o));
  BYTE_REGISTER byte_register_8 (
    .contents(out_120), .row__n(decoder_4x16_1_out_9), .\input (\input ), .col__m(decoder_4x16_2_msb),
    .reset(reset), .set__write_mode(set), .enable__read_mode(enable), .\output (o));
  BYTE_REGISTER byte_register_9 (
    .contents(out_136), .row__n(decoder_4x16_1_out_10), .\input (\input ), .col__m(decoder_4x16_2_msb),
    .reset(reset), .set__write_mode(set), .enable__read_mode(enable), .\output (o));
  BYTE_REGISTER byte_register_10 (
    .contents(out_152), .row__n(decoder_4x16_1_out_11), .\input (\input ), .col__m(decoder_4x16_2_msb),
    .reset(reset), .set__write_mode(set), .enable__read_mode(enable), .\output (o));
  BYTE_REGISTER byte_register_11 (
    .contents(out_168), .row__n(decoder_4x16_1_out_12), .\input (\input ), .col__m(decoder_4x16_2_msb),
    .reset(reset), .set__write_mode(set), .enable__read_mode(enable), .\output (o));
  BYTE_REGISTER byte_register_12 (
    .contents(out_184), .row__n(decoder_4x16_1_out_13), .\input (\input ), .col__m(decoder_4x16_2_msb),
    .reset(reset), .set__write_mode(set), .enable__read_mode(enable), .\output (o));
  BYTE_REGISTER byte_register_13 (
    .contents(out_200), .row__n(decoder_4x16_1_out_14), .\input (\input ), .col__m(decoder_4x16_2_msb),
    .reset(reset), .set__write_mode(set), .enable__read_mode(enable), .\output (o));
  BYTE_REGISTER byte_register_14 (
    .contents(out_216), .row__n(decoder_4x16_1_out_15), .\input (\input ), .col__m(decoder_4x16_2_msb),
    .reset(reset), .set__write_mode(set), .enable__read_mode(enable), .\output (o));
  BYTE_REGISTER byte_register_15 (
    .contents(out_232), .row__n(decoder_4x16_1_out_16), .\input (\input ), .col__m(decoder_4x16_2_msb),
    .reset(reset), .set__write_mode(set), .enable__read_mode(enable), .\output (o));
  BYTE_REGISTER byte_register_16 (
    .contents(out_248), .row__n(decoder_4x16_1_msb), .\input (\input ), .col__m(decoder_4x16_2_msb),
    .reset(reset), .set__write_mode(set), .enable__read_mode(enable), .\output (o));
  BYTE_REGISTER byte_register_17 (
    .contents(out_9), .row__n(decoder_4x16_1_lsb), .\input (\input ), .col__m(decoder_4x16_2_out_16),
    .reset(reset), .set__write_mode(set), .enable__read_mode(enable), .\output (o));
  BYTE_REGISTER byte_register_18 (
    .contents(out_25), .row__n(decoder_4x16_1_out_3), .\input (\input ), .col__m(decoder_4x16_2_out_16),
    .reset(reset), .set__write_mode(set), .enable__read_mode(enable), .\output (o));
  BYTE_REGISTER byte_register_19 (
    .contents(out_41), .row__n(decoder_4x16_1_out_4), .\input (\input ), .col__m(decoder_4x16_2_out_16),
    .reset(reset), .set__write_mode(set), .enable__read_mode(enable), .\output (o));
  BYTE_REGISTER byte_register_20 (
    .contents(out_57), .row__n(decoder_4x16_1_out_5), .\input (\input ), .col__m(decoder_4x16_2_out_16),
    .reset(reset), .set__write_mode(set), .enable__read_mode(enable), .\output (o));
  BYTE_REGISTER byte_register_21 (
    .contents(out_73), .row__n(decoder_4x16_1_out_6), .\input (\input ), .col__m(decoder_4x16_2_out_16),
    .reset(reset), .set__write_mode(set), .enable__read_mode(enable), .\output (o));
  BYTE_REGISTER byte_register_22 (
    .contents(out_89), .row__n(decoder_4x16_1_out_7), .\input (\input ), .col__m(decoder_4x16_2_out_16),
    .reset(reset), .set__write_mode(set), .enable__read_mode(enable), .\output (o));
  BYTE_REGISTER byte_register_23 (
    .contents(out_105), .row__n(decoder_4x16_1_out_8), .\input (\input ), .col__m(decoder_4x16_2_out_16),
    .reset(reset), .set__write_mode(set), .enable__read_mode(enable), .\output (o));
  BYTE_REGISTER byte_register_24 (
    .contents(out_121), .row__n(decoder_4x16_1_out_9), .\input (\input ), .col__m(decoder_4x16_2_out_16),
    .reset(reset), .set__write_mode(set), .enable__read_mode(enable), .\output (o));
  BYTE_REGISTER byte_register_25 (
    .contents(out_137), .row__n(decoder_4x16_1_out_10), .\input (\input ), .col__m(decoder_4x16_2_out_16),
    .reset(reset), .set__write_mode(set), .enable__read_mode(enable), .\output (o));
  BYTE_REGISTER byte_register_26 (
    .contents(out_153), .row__n(decoder_4x16_1_out_11), .\input (\input ), .col__m(decoder_4x16_2_out_16),
    .reset(reset), .set__write_mode(set), .enable__read_mode(enable), .\output (o));
  BYTE_REGISTER byte_register_27 (
    .contents(out_169), .row__n(decoder_4x16_1_out_12), .\input (\input ), .col__m(decoder_4x16_2_out_16),
    .reset(reset), .set__write_mode(set), .enable__read_mode(enable), .\output (o));
  BYTE_REGISTER byte_register_28 (
    .contents(out_185), .row__n(decoder_4x16_1_out_13), .\input (\input ), .col__m(decoder_4x16_2_out_16),
    .reset(reset), .set__write_mode(set), .enable__read_mode(enable), .\output (o));
  BYTE_REGISTER byte_register_29 (
    .contents(out_201), .row__n(decoder_4x16_1_out_14), .\input (\input ), .col__m(decoder_4x16_2_out_16),
    .reset(reset), .set__write_mode(set), .enable__read_mode(enable), .\output (o));
  BYTE_REGISTER byte_register_30 (
    .contents(out_217), .row__n(decoder_4x16_1_out_15), .\input (\input ), .col__m(decoder_4x16_2_out_16),
    .reset(reset), .set__write_mode(set), .enable__read_mode(enable), .\output (o));
  BYTE_REGISTER byte_register_31 (
    .contents(out_233), .row__n(decoder_4x16_1_out_16), .\input (\input ), .col__m(decoder_4x16_2_out_16),
    .reset(reset), .set__write_mode(set), .enable__read_mode(enable), .\output (o));
  BYTE_REGISTER byte_register_32 (
    .contents(out_249), .row__n(decoder_4x16_1_msb), .\input (\input ), .col__m(decoder_4x16_2_out_16),
    .reset(reset), .set__write_mode(set), .enable__read_mode(enable), .\output (o));
  BYTE_REGISTER byte_register_33 (
    .contents(out_10), .row__n(decoder_4x16_1_lsb), .\input (\input ), .col__m(decoder_4x16_2_out_15),
    .reset(reset), .set__write_mode(set), .enable__read_mode(enable), .\output (o));
  BYTE_REGISTER byte_register_34 (
    .contents(out_26), .row__n(decoder_4x16_1_out_3), .\input (\input ), .col__m(decoder_4x16_2_out_15),
    .reset(reset), .set__write_mode(set), .enable__read_mode(enable), .\output (o));
  BYTE_REGISTER byte_register_35 (
    .contents(out_42), .row__n(decoder_4x16_1_out_4), .\input (\input ), .col__m(decoder_4x16_2_out_15),
    .reset(reset), .set__write_mode(set), .enable__read_mode(enable), .\output (o));
  BYTE_REGISTER byte_register_36 (
    .contents(out_58), .row__n(decoder_4x16_1_out_5), .\input (\input ), .col__m(decoder_4x16_2_out_15),
    .reset(reset), .set__write_mode(set), .enable__read_mode(enable), .\output (o));
  BYTE_REGISTER byte_register_37 (
    .contents(out_74), .row__n(decoder_4x16_1_out_6), .\input (\input ), .col__m(decoder_4x16_2_out_15),
    .reset(reset), .set__write_mode(set), .enable__read_mode(enable), .\output (o));
  BYTE_REGISTER byte_register_38 (
    .contents(out_90), .row__n(decoder_4x16_1_out_7), .\input (\input ), .col__m(decoder_4x16_2_out_15),
    .reset(reset), .set__write_mode(set), .enable__read_mode(enable), .\output (o));
  BYTE_REGISTER byte_register_39 (
    .contents(out_106), .row__n(decoder_4x16_1_out_8), .\input (\input ), .col__m(decoder_4x16_2_out_15),
    .reset(reset), .set__write_mode(set), .enable__read_mode(enable), .\output (o));
  BYTE_REGISTER byte_register_40 (
    .contents(out_122), .row__n(decoder_4x16_1_out_9), .\input (\input ), .col__m(decoder_4x16_2_out_15),
    .reset(reset), .set__write_mode(set), .enable__read_mode(enable), .\output (o));
  BYTE_REGISTER byte_register_41 (
    .contents(out_138), .row__n(decoder_4x16_1_out_10), .\input (\input ), .col__m(decoder_4x16_2_out_15),
    .reset(reset), .set__write_mode(set), .enable__read_mode(enable), .\output (o));
  BYTE_REGISTER byte_register_42 (
    .contents(out_154), .row__n(decoder_4x16_1_out_11), .\input (\input ), .col__m(decoder_4x16_2_out_15),
    .reset(reset), .set__write_mode(set), .enable__read_mode(enable), .\output (o));
  BYTE_REGISTER byte_register_43 (
    .contents(out_170), .row__n(decoder_4x16_1_out_12), .\input (\input ), .col__m(decoder_4x16_2_out_15),
    .reset(reset), .set__write_mode(set), .enable__read_mode(enable), .\output (o));
  BYTE_REGISTER byte_register_44 (
    .contents(out_186), .row__n(decoder_4x16_1_out_13), .\input (\input ), .col__m(decoder_4x16_2_out_15),
    .reset(reset), .set__write_mode(set), .enable__read_mode(enable), .\output (o));
  BYTE_REGISTER byte_register_45 (
    .contents(out_202), .row__n(decoder_4x16_1_out_14), .\input (\input ), .col__m(decoder_4x16_2_out_15),
    .reset(reset), .set__write_mode(set), .enable__read_mode(enable), .\output (o));
  BYTE_REGISTER byte_register_46 (
    .contents(out_218), .row__n(decoder_4x16_1_out_15), .\input (\input ), .col__m(decoder_4x16_2_out_15),
    .reset(reset), .set__write_mode(set), .enable__read_mode(enable), .\output (o));
  BYTE_REGISTER byte_register_47 (
    .contents(out_234), .row__n(decoder_4x16_1_out_16), .\input (\input ), .col__m(decoder_4x16_2_out_15),
    .reset(reset), .set__write_mode(set), .enable__read_mode(enable), .\output (o));
  BYTE_REGISTER byte_register_48 (
    .contents(out_250), .row__n(decoder_4x16_1_msb), .\input (\input ), .col__m(decoder_4x16_2_out_15),
    .reset(reset), .set__write_mode(set), .enable__read_mode(enable), .\output (o));
  BYTE_REGISTER byte_register_49 (
    .contents(out_11), .row__n(decoder_4x16_1_lsb), .\input (\input ), .col__m(decoder_4x16_2_out_14),
    .reset(reset), .set__write_mode(set), .enable__read_mode(enable), .\output (o));
  BYTE_REGISTER byte_register_50 (
    .contents(out_27), .row__n(decoder_4x16_1_out_3), .\input (\input ), .col__m(decoder_4x16_2_out_14),
    .reset(reset), .set__write_mode(set), .enable__read_mode(enable), .\output (o));
  BYTE_REGISTER byte_register_51 (
    .contents(out_43), .row__n(decoder_4x16_1_out_4), .\input (\input ), .col__m(decoder_4x16_2_out_14),
    .reset(reset), .set__write_mode(set), .enable__read_mode(enable), .\output (o));
  BYTE_REGISTER byte_register_52 (
    .contents(out_59), .row__n(decoder_4x16_1_out_5), .\input (\input ), .col__m(decoder_4x16_2_out_14),
    .reset(reset), .set__write_mode(set), .enable__read_mode(enable), .\output (o));
  BYTE_REGISTER byte_register_53 (
    .contents(out_75), .row__n(decoder_4x16_1_out_6), .\input (\input ), .col__m(decoder_4x16_2_out_14),
    .reset(reset), .set__write_mode(set), .enable__read_mode(enable), .\output (o));
  BYTE_REGISTER byte_register_54 (
    .contents(out_91), .row__n(decoder_4x16_1_out_7), .\input (\input ), .col__m(decoder_4x16_2_out_14),
    .reset(reset), .set__write_mode(set), .enable__read_mode(enable), .\output (o));
  BYTE_REGISTER byte_register_55 (
    .contents(out_107), .row__n(decoder_4x16_1_out_8), .\input (\input ), .col__m(decoder_4x16_2_out_14),
    .reset(reset), .set__write_mode(set), .enable__read_mode(enable), .\output (o));
  BYTE_REGISTER byte_register_56 (
    .contents(out_123), .row__n(decoder_4x16_1_out_9), .\input (\input ), .col__m(decoder_4x16_2_out_14),
    .reset(reset), .set__write_mode(set), .enable__read_mode(enable), .\output (o));
  BYTE_REGISTER byte_register_57 (
    .contents(out_139), .row__n(decoder_4x16_1_out_10), .\input (\input ), .col__m(decoder_4x16_2_out_14),
    .reset(reset), .set__write_mode(set), .enable__read_mode(enable), .\output (o));
  BYTE_REGISTER byte_register_58 (
    .contents(out_155), .row__n(decoder_4x16_1_out_11), .\input (\input ), .col__m(decoder_4x16_2_out_14),
    .reset(reset), .set__write_mode(set), .enable__read_mode(enable), .\output (o));
  BYTE_REGISTER byte_register_59 (
    .contents(out_171), .row__n(decoder_4x16_1_out_12), .\input (\input ), .col__m(decoder_4x16_2_out_14),
    .reset(reset), .set__write_mode(set), .enable__read_mode(enable), .\output (o));
  BYTE_REGISTER byte_register_60 (
    .contents(out_187), .row__n(decoder_4x16_1_out_13), .\input (\input ), .col__m(decoder_4x16_2_out_14),
    .reset(reset), .set__write_mode(set), .enable__read_mode(enable), .\output (o));
  BYTE_REGISTER byte_register_61 (
    .contents(out_203), .row__n(decoder_4x16_1_out_14), .\input (\input ), .col__m(decoder_4x16_2_out_14),
    .reset(reset), .set__write_mode(set), .enable__read_mode(enable), .\output (o));
  BYTE_REGISTER byte_register_62 (
    .contents(out_219), .row__n(decoder_4x16_1_out_15), .\input (\input ), .col__m(decoder_4x16_2_out_14),
    .reset(reset), .set__write_mode(set), .enable__read_mode(enable), .\output (o));
  BYTE_REGISTER byte_register_63 (
    .contents(out_235), .row__n(decoder_4x16_1_out_16), .\input (\input ), .col__m(decoder_4x16_2_out_14),
    .reset(reset), .set__write_mode(set), .enable__read_mode(enable), .\output (o));
  BYTE_REGISTER byte_register_64 (
    .contents(out_251), .row__n(decoder_4x16_1_msb), .\input (\input ), .col__m(decoder_4x16_2_out_14),
    .reset(reset), .set__write_mode(set), .enable__read_mode(enable), .\output (o));
  BYTE_REGISTER byte_register_65 (
    .contents(out_12), .row__n(decoder_4x16_1_lsb), .\input (\input ), .col__m(decoder_4x16_2_out_13),
    .reset(reset), .set__write_mode(set), .enable__read_mode(enable), .\output (o));
  BYTE_REGISTER byte_register_66 (
    .contents(out_28), .row__n(decoder_4x16_1_out_3), .\input (\input ), .col__m(decoder_4x16_2_out_13),
    .reset(reset), .set__write_mode(set), .enable__read_mode(enable), .\output (o));
  BYTE_REGISTER byte_register_67 (
    .contents(out_44), .row__n(decoder_4x16_1_out_4), .\input (\input ), .col__m(decoder_4x16_2_out_13),
    .reset(reset), .set__write_mode(set), .enable__read_mode(enable), .\output (o));
  BYTE_REGISTER byte_register_68 (
    .contents(out_60), .row__n(decoder_4x16_1_out_5), .\input (\input ), .col__m(decoder_4x16_2_out_13),
    .reset(reset), .set__write_mode(set), .enable__read_mode(enable), .\output (o));
  BYTE_REGISTER byte_register_69 (
    .contents(out_76), .row__n(decoder_4x16_1_out_6), .\input (\input ), .col__m(decoder_4x16_2_out_13),
    .reset(reset), .set__write_mode(set), .enable__read_mode(enable), .\output (o));
  BYTE_REGISTER byte_register_70 (
    .contents(out_92), .row__n(decoder_4x16_1_out_7), .\input (\input ), .col__m(decoder_4x16_2_out_13),
    .reset(reset), .set__write_mode(set), .enable__read_mode(enable), .\output (o));
  BYTE_REGISTER byte_register_71 (
    .contents(out_108), .row__n(decoder_4x16_1_out_8), .\input (\input ), .col__m(decoder_4x16_2_out_13),
    .reset(reset), .set__write_mode(set), .enable__read_mode(enable), .\output (o));
  BYTE_REGISTER byte_register_72 (
    .contents(out_124), .row__n(decoder_4x16_1_out_9), .\input (\input ), .col__m(decoder_4x16_2_out_13),
    .reset(reset), .set__write_mode(set), .enable__read_mode(enable), .\output (o));
  BYTE_REGISTER byte_register_73 (
    .contents(out_140), .row__n(decoder_4x16_1_out_10), .\input (\input ), .col__m(decoder_4x16_2_out_13),
    .reset(reset), .set__write_mode(set), .enable__read_mode(enable), .\output (o));
  BYTE_REGISTER byte_register_74 (
    .contents(out_156), .row__n(decoder_4x16_1_out_11), .\input (\input ), .col__m(decoder_4x16_2_out_13),
    .reset(reset), .set__write_mode(set), .enable__read_mode(enable), .\output (o));
  BYTE_REGISTER byte_register_75 (
    .contents(out_172), .row__n(decoder_4x16_1_out_12), .\input (\input ), .col__m(decoder_4x16_2_out_13),
    .reset(reset), .set__write_mode(set), .enable__read_mode(enable), .\output (o));
  BYTE_REGISTER byte_register_76 (
    .contents(out_188), .row__n(decoder_4x16_1_out_13), .\input (\input ), .col__m(decoder_4x16_2_out_13),
    .reset(reset), .set__write_mode(set), .enable__read_mode(enable), .\output (o));
  BYTE_REGISTER byte_register_77 (
    .contents(out_204), .row__n(decoder_4x16_1_out_14), .\input (\input ), .col__m(decoder_4x16_2_out_13),
    .reset(reset), .set__write_mode(set), .enable__read_mode(enable), .\output (o));
  BYTE_REGISTER byte_register_78 (
    .contents(out_220), .row__n(decoder_4x16_1_out_15), .\input (\input ), .col__m(decoder_4x16_2_out_13),
    .reset(reset), .set__write_mode(set), .enable__read_mode(enable), .\output (o));
  BYTE_REGISTER byte_register_79 (
    .contents(out_236), .row__n(decoder_4x16_1_out_16), .\input (\input ), .col__m(decoder_4x16_2_out_13),
    .reset(reset), .set__write_mode(set), .enable__read_mode(enable), .\output (o));
  BYTE_REGISTER byte_register_80 (
    .contents(out_252), .row__n(decoder_4x16_1_msb), .\input (\input ), .col__m(decoder_4x16_2_out_13),
    .reset(reset), .set__write_mode(set), .enable__read_mode(enable), .\output (o));
  BYTE_REGISTER byte_register_81 (
    .contents(out_13), .row__n(decoder_4x16_1_lsb), .\input (\input ), .col__m(decoder_4x16_2_out_12),
    .reset(reset), .set__write_mode(set), .enable__read_mode(enable), .\output (o));
  BYTE_REGISTER byte_register_82 (
    .contents(out_29), .row__n(decoder_4x16_1_out_3), .\input (\input ), .col__m(decoder_4x16_2_out_12),
    .reset(reset), .set__write_mode(set), .enable__read_mode(enable), .\output (o));
  BYTE_REGISTER byte_register_83 (
    .contents(out_45), .row__n(decoder_4x16_1_out_4), .\input (\input ), .col__m(decoder_4x16_2_out_12),
    .reset(reset), .set__write_mode(set), .enable__read_mode(enable), .\output (o));
  BYTE_REGISTER byte_register_84 (
    .contents(out_61), .row__n(decoder_4x16_1_out_5), .\input (\input ), .col__m(decoder_4x16_2_out_12),
    .reset(reset), .set__write_mode(set), .enable__read_mode(enable), .\output (o));
  BYTE_REGISTER byte_register_85 (
    .contents(out_77), .row__n(decoder_4x16_1_out_6), .\input (\input ), .col__m(decoder_4x16_2_out_12),
    .reset(reset), .set__write_mode(set), .enable__read_mode(enable), .\output (o));
  BYTE_REGISTER byte_register_86 (
    .contents(out_93), .row__n(decoder_4x16_1_out_7), .\input (\input ), .col__m(decoder_4x16_2_out_12),
    .reset(reset), .set__write_mode(set), .enable__read_mode(enable), .\output (o));
  BYTE_REGISTER byte_register_87 (
    .contents(out_109), .row__n(decoder_4x16_1_out_8), .\input (\input ), .col__m(decoder_4x16_2_out_12),
    .reset(reset), .set__write_mode(set), .enable__read_mode(enable), .\output (o));
  BYTE_REGISTER byte_register_88 (
    .contents(out_125), .row__n(decoder_4x16_1_out_9), .\input (\input ), .col__m(decoder_4x16_2_out_12),
    .reset(reset), .set__write_mode(set), .enable__read_mode(enable), .\output (o));
  BYTE_REGISTER byte_register_89 (
    .contents(out_141), .row__n(decoder_4x16_1_out_10), .\input (\input ), .col__m(decoder_4x16_2_out_12),
    .reset(reset), .set__write_mode(set), .enable__read_mode(enable), .\output (o));
  BYTE_REGISTER byte_register_90 (
    .contents(out_157), .row__n(decoder_4x16_1_out_11), .\input (\input ), .col__m(decoder_4x16_2_out_12),
    .reset(reset), .set__write_mode(set), .enable__read_mode(enable), .\output (o));
  BYTE_REGISTER byte_register_91 (
    .contents(out_173), .row__n(decoder_4x16_1_out_12), .\input (\input ), .col__m(decoder_4x16_2_out_12),
    .reset(reset), .set__write_mode(set), .enable__read_mode(enable), .\output (o));
  BYTE_REGISTER byte_register_92 (
    .contents(out_189), .row__n(decoder_4x16_1_out_13), .\input (\input ), .col__m(decoder_4x16_2_out_12),
    .reset(reset), .set__write_mode(set), .enable__read_mode(enable), .\output (o));
  BYTE_REGISTER byte_register_93 (
    .contents(out_205), .row__n(decoder_4x16_1_out_14), .\input (\input ), .col__m(decoder_4x16_2_out_12),
    .reset(reset), .set__write_mode(set), .enable__read_mode(enable), .\output (o));
  BYTE_REGISTER byte_register_94 (
    .contents(out_221), .row__n(decoder_4x16_1_out_15), .\input (\input ), .col__m(decoder_4x16_2_out_12),
    .reset(reset), .set__write_mode(set), .enable__read_mode(enable), .\output (o));
  BYTE_REGISTER byte_register_95 (
    .contents(out_237), .row__n(decoder_4x16_1_out_16), .\input (\input ), .col__m(decoder_4x16_2_out_12),
    .reset(reset), .set__write_mode(set), .enable__read_mode(enable), .\output (o));
  BYTE_REGISTER byte_register_96 (
    .contents(out_253), .row__n(decoder_4x16_1_msb), .\input (\input ), .col__m(decoder_4x16_2_out_12),
    .reset(reset), .set__write_mode(set), .enable__read_mode(enable), .\output (o));
  BYTE_REGISTER byte_register_97 (
    .contents(out_14), .row__n(decoder_4x16_1_lsb), .\input (\input ), .col__m(byte_register_110_p3),
    .reset(reset), .set__write_mode(set), .enable__read_mode(enable), .\output (o));
  BYTE_REGISTER byte_register_98 (
    .contents(out_30), .row__n(decoder_4x16_1_out_3), .col__m(byte_register_110_p3), .reset(reset),
    .set__write_mode(set), .enable__read_mode(enable), .\output (o));  // open: input
  BYTE_REGISTER byte_register_99 (
    .contents(out_46), .row__n(decoder_4x16_1_out_4), .\input (\input ), .col__m(byte_register_110_p3),
    .reset(reset), .set__write_mode(set), .enable__read_mode(enable), .\output (o));
  BYTE_REGISTER byte_register_100 (
    .contents(out_62), .row__n(decoder_4x16_1_out_5), .\input (\input ), .col__m(byte_register_110_p3),
    .reset(reset), .set__write_mode(set), .enable__read_mode(enable), .\output (o));
  BYTE_REGISTER byte_register_101 (
    .contents(out_78), .row__n(decoder_4x16_1_out_6), .\input (\input ), .col__m(byte_register_110_p3),
    .reset(reset), .set__write_mode(set), .enable__read_mode(enable), .\output (o));
  BYTE_REGISTER byte_register_102 (
    .contents(out_94), .row__n(decoder_4x16_1_out_7), .\input (\input ), .col__m(byte_register_110_p3),
    .reset(reset), .set__write_mode(set), .enable__read_mode(enable), .\output (o));
  BYTE_REGISTER byte_register_103 (
    .contents(out_110), .row__n(decoder_4x16_1_out_8), .\input (\input ), .col__m(byte_register_110_p3),
    .reset(reset), .set__write_mode(set), .enable__read_mode(enable), .\output (o));
  BYTE_REGISTER byte_register_104 (
    .contents(out_126), .row__n(decoder_4x16_1_out_9), .\input (\input ), .col__m(byte_register_110_p3),
    .reset(reset), .set__write_mode(set), .enable__read_mode(enable), .\output (o));
  BYTE_REGISTER byte_register_105 (
    .contents(out_142), .row__n(decoder_4x16_1_out_10), .\input (\input ), .col__m(byte_register_110_p3),
    .reset(reset), .set__write_mode(set), .enable__read_mode(enable), .\output (o));
  BYTE_REGISTER byte_register_106 (
    .contents(out_158), .row__n(decoder_4x16_1_out_11), .\input (\input ), .col__m(byte_register_110_p3),
    .reset(reset), .set__write_mode(set), .enable__read_mode(enable), .\output (o));
  BYTE_REGISTER byte_register_107 (
    .contents(out_174), .row__n(decoder_4x16_1_out_12), .\input (\input ), .col__m(byte_register_110_p3),
    .reset(reset), .set__write_mode(set), .enable__read_mode(enable), .\output (o));
  BYTE_REGISTER byte_register_108 (
    .contents(out_190), .row__n(decoder_4x16_1_out_13), .\input (\input ), .col__m(byte_register_110_p3),
    .reset(reset), .set__write_mode(set), .enable__read_mode(enable), .\output (o));
  BYTE_REGISTER byte_register_109 (
    .contents(out_206), .row__n(decoder_4x16_1_out_14), .\input (\input ), .col__m(byte_register_110_p3),
    .reset(reset), .set__write_mode(set), .enable__read_mode(enable), .\output (o));
  // BYTE_REGISTER byte_register_110: pin names not known; wires that end beside it: decoder_4x16_1_out_15, \input , byte_register_110_p3, set, out_222, enable, reset, o
  BYTE_REGISTER byte_register_111 (
    .contents(out_238), .row__n(decoder_4x16_1_out_16), .\input (\input ), .col__m(byte_register_110_p3),
    .reset(reset), .set__write_mode(set), .enable__read_mode(enable), .\output (o));
  BYTE_REGISTER byte_register_112 (
    .contents(out_254), .row__n(decoder_4x16_1_msb), .\input (\input ), .col__m(byte_register_110_p3),
    .reset(reset), .set__write_mode(set), .enable__read_mode(enable), .\output (o));
  DECODER_4x16 decoder_4x16_2 (
    .\input (mem_8_1_out_3[3:0]), .LSB(decoder_4x16_2_lsb), .out_3(decoder_4x16_2_out_3),
    .out_4(decoder_4x16_2_out_4), .out_5(decoder_4x16_2_out_5), .out_6(decoder_4x16_2_out_6),
    .out_7(decoder_4x16_2_out_7), .out_8(decoder_4x16_2_out_8), .out_9(decoder_4x16_2_out_9),
    .out_10(decoder_4x16_2_out_10), .out_11(byte_register_110_p3), .out_12(decoder_4x16_2_out_12),
    .out_13(decoder_4x16_2_out_13), .out_14(decoder_4x16_2_out_14), .out_15(decoder_4x16_2_out_15),
    .out_16(decoder_4x16_2_out_16), .MSB(decoder_4x16_2_msb));
  BYTE_REGISTER byte_register_113 (
    .contents(out_15), .row__n(decoder_4x16_1_lsb), .\input (\input ), .col__m(decoder_4x16_2_out_10),
    .reset(reset), .set__write_mode(set), .enable__read_mode(enable), .\output (o));
  BYTE_REGISTER byte_register_114 (
    .contents(out_31), .row__n(decoder_4x16_1_out_3), .\input (\input ), .col__m(decoder_4x16_2_out_10),
    .reset(reset), .set__write_mode(set), .enable__read_mode(enable), .\output (o));
  BYTE_REGISTER byte_register_115 (
    .contents(out_47), .row__n(decoder_4x16_1_out_4), .\input (\input ), .col__m(decoder_4x16_2_out_10),
    .reset(reset), .set__write_mode(set), .enable__read_mode(enable), .\output (o));
  BYTE_REGISTER byte_register_116 (
    .contents(out_63), .row__n(decoder_4x16_1_out_5), .\input (\input ), .col__m(decoder_4x16_2_out_10),
    .reset(reset), .set__write_mode(set), .enable__read_mode(enable), .\output (o));
  BYTE_REGISTER byte_register_117 (
    .contents(out_79), .row__n(decoder_4x16_1_out_6), .\input (\input ), .col__m(decoder_4x16_2_out_10),
    .reset(reset), .set__write_mode(set), .enable__read_mode(enable), .\output (o));
  BYTE_REGISTER byte_register_118 (
    .contents(out_95), .row__n(decoder_4x16_1_out_7), .\input (\input ), .col__m(decoder_4x16_2_out_10),
    .reset(reset), .set__write_mode(set), .enable__read_mode(enable), .\output (o));
  BYTE_REGISTER byte_register_119 (
    .contents(out_111), .row__n(decoder_4x16_1_out_8), .\input (\input ), .col__m(decoder_4x16_2_out_10),
    .reset(reset), .set__write_mode(set), .enable__read_mode(enable), .\output (o));
  BYTE_REGISTER byte_register_120 (
    .contents(out_127), .row__n(decoder_4x16_1_out_9), .\input (\input ), .col__m(decoder_4x16_2_out_10),
    .reset(reset), .set__write_mode(set), .enable__read_mode(enable), .\output (o));
  // BYTE_REGISTER byte_register_121: pin names not known; wires that end beside it: decoder_4x16_1_out_10, \input , decoder_4x16_2_out_10, set, out_143, enable, reset, o
  BYTE_REGISTER byte_register_122 (
    .contents(out_159), .row__n(decoder_4x16_1_out_11), .\input (\input ), .col__m(decoder_4x16_2_out_10),
    .reset(reset), .set__write_mode(set), .enable__read_mode(enable), .\output (o));
  BYTE_REGISTER byte_register_123 (
    .contents(out_175), .row__n(decoder_4x16_1_out_12), .\input (\input ), .col__m(decoder_4x16_2_out_10),
    .reset(reset), .set__write_mode(set), .enable__read_mode(enable), .\output (o));
  BYTE_REGISTER byte_register_124 (
    .contents(out_191), .row__n(decoder_4x16_1_out_13), .\input (\input ), .col__m(decoder_4x16_2_out_10),
    .reset(reset), .set__write_mode(set), .enable__read_mode(enable), .\output (o));
  BYTE_REGISTER byte_register_125 (
    .contents(out_207), .row__n(decoder_4x16_1_out_14), .\input (\input ), .col__m(decoder_4x16_2_out_10),
    .reset(reset), .set__write_mode(set), .enable__read_mode(enable), .\output (o));
  BYTE_REGISTER byte_register_126 (
    .contents(out_223), .row__n(decoder_4x16_1_out_15), .\input (\input ), .col__m(decoder_4x16_2_out_10),
    .reset(reset), .set__write_mode(set), .enable__read_mode(enable), .\output (o));
  BYTE_REGISTER byte_register_127 (
    .contents(out_239), .row__n(decoder_4x16_1_out_16), .\input (\input ), .col__m(decoder_4x16_2_out_10),
    .reset(reset), .set__write_mode(set), .enable__read_mode(enable), .\output (o));
  BYTE_REGISTER byte_register_128 (
    .contents(out_255), .row__n(decoder_4x16_1_msb), .\input (\input ), .col__m(decoder_4x16_2_out_10),
    .reset(reset), .set__write_mode(set), .enable__read_mode(enable), .\output (o));
  BYTE_REGISTER byte_register_129 (
    .contents(out_16), .row__n(decoder_4x16_1_lsb), .\input (\input ), .col__m(decoder_4x16_2_out_9),
    .reset(reset), .set__write_mode(set), .enable__read_mode(enable), .\output (o));
  BYTE_REGISTER byte_register_130 (
    .contents(out_32), .row__n(decoder_4x16_1_out_3), .\input (\input ), .col__m(decoder_4x16_2_out_9),
    .reset(reset), .set__write_mode(set), .enable__read_mode(enable), .\output (o));
  BYTE_REGISTER byte_register_131 (
    .contents(out_48), .row__n(decoder_4x16_1_out_4), .\input (\input ), .col__m(decoder_4x16_2_out_9),
    .reset(reset), .set__write_mode(set), .enable__read_mode(enable), .\output (o));
  BYTE_REGISTER byte_register_132 (
    .contents(out_64), .row__n(decoder_4x16_1_out_5), .\input (\input ), .col__m(decoder_4x16_2_out_9),
    .reset(reset), .set__write_mode(set), .enable__read_mode(enable), .\output (o));
  BYTE_REGISTER byte_register_133 (
    .contents(out_80), .row__n(decoder_4x16_1_out_6), .\input (\input ), .col__m(decoder_4x16_2_out_9),
    .reset(reset), .set__write_mode(set), .enable__read_mode(enable), .\output (o));
  BYTE_REGISTER byte_register_134 (
    .contents(out_96), .row__n(decoder_4x16_1_out_7), .\input (\input ), .col__m(decoder_4x16_2_out_9),
    .reset(reset), .set__write_mode(set), .enable__read_mode(enable), .\output (o));
  BYTE_REGISTER byte_register_135 (
    .contents(out_112), .row__n(decoder_4x16_1_out_8), .\input (\input ), .col__m(decoder_4x16_2_out_9),
    .reset(reset), .set__write_mode(set), .enable__read_mode(enable), .\output (o));
  BYTE_REGISTER byte_register_136 (
    .contents(out_128), .row__n(decoder_4x16_1_out_9), .\input (\input ), .col__m(decoder_4x16_2_out_9),
    .reset(reset), .set__write_mode(set), .enable__read_mode(enable), .\output (o));
  BYTE_REGISTER byte_register_137 (
    .contents(out_144), .row__n(decoder_4x16_1_out_10), .\input (\input ), .col__m(decoder_4x16_2_out_9),
    .reset(reset), .set__write_mode(set), .enable__read_mode(enable), .\output (o));
  BYTE_REGISTER byte_register_138 (
    .contents(out_160), .row__n(decoder_4x16_1_out_11), .\input (\input ), .col__m(decoder_4x16_2_out_9),
    .reset(reset), .set__write_mode(set), .enable__read_mode(enable), .\output (o));
  BYTE_REGISTER byte_register_139 (
    .contents(out_176), .row__n(decoder_4x16_1_out_12), .\input (\input ), .col__m(decoder_4x16_2_out_9),
    .reset(reset), .set__write_mode(set), .enable__read_mode(enable), .\output (o));
  BYTE_REGISTER byte_register_140 (
    .contents(out_192), .row__n(decoder_4x16_1_out_13), .\input (\input ), .col__m(decoder_4x16_2_out_9),
    .reset(reset), .set__write_mode(set), .enable__read_mode(enable), .\output (o));
  BYTE_REGISTER byte_register_141 (
    .contents(out_208), .row__n(decoder_4x16_1_out_14), .\input (\input ), .col__m(decoder_4x16_2_out_9),
    .reset(reset), .set__write_mode(set), .enable__read_mode(enable), .\output (o));
  BYTE_REGISTER byte_register_142 (
    .contents(out_224), .row__n(decoder_4x16_1_out_15), .\input (\input ), .col__m(decoder_4x16_2_out_9),
    .reset(reset), .set__write_mode(set), .enable__read_mode(enable), .\output (o));
  BYTE_REGISTER byte_register_143 (
    .contents(out_240), .row__n(decoder_4x16_1_out_16), .\input (\input ), .col__m(decoder_4x16_2_out_9),
    .reset(reset), .set__write_mode(set), .enable__read_mode(enable), .\output (o));
  BYTE_REGISTER byte_register_144 (
    .contents(out_256), .row__n(decoder_4x16_1_msb), .\input (\input ), .col__m(decoder_4x16_2_out_9),
    .reset(reset), .set__write_mode(set), .enable__read_mode(enable), .\output (o));
  BYTE_REGISTER byte_register_145 (
    .contents(out_17), .row__n(decoder_4x16_1_lsb), .\input (\input ), .col__m(decoder_4x16_2_out_8),
    .reset(reset), .set__write_mode(set), .enable__read_mode(enable));  // open: output
  BYTE_REGISTER byte_register_146 (
    .contents(out_33), .row__n(decoder_4x16_1_out_3), .\input (\input ), .col__m(decoder_4x16_2_out_8),
    .reset(reset), .set__write_mode(set), .enable__read_mode(enable));  // open: output
  BYTE_REGISTER byte_register_147 (
    .contents(out_49), .row__n(decoder_4x16_1_out_4), .\input (\input ), .col__m(decoder_4x16_2_out_8),
    .reset(reset), .set__write_mode(set), .enable__read_mode(enable));  // open: output
  BYTE_REGISTER byte_register_148 (
    .contents(out_65), .row__n(decoder_4x16_1_out_5), .\input (\input ), .col__m(decoder_4x16_2_out_8),
    .reset(reset), .set__write_mode(set), .enable__read_mode(enable));  // open: output
  BYTE_REGISTER byte_register_149 (
    .contents(out_81), .row__n(decoder_4x16_1_out_6), .\input (\input ), .col__m(decoder_4x16_2_out_8),
    .reset(reset), .set__write_mode(set), .enable__read_mode(enable));  // open: output
  BYTE_REGISTER byte_register_150 (
    .contents(out_97), .row__n(decoder_4x16_1_out_7), .\input (\input ), .col__m(decoder_4x16_2_out_8),
    .reset(reset), .set__write_mode(set), .enable__read_mode(enable));  // open: output
  BYTE_REGISTER byte_register_151 (
    .contents(out_113), .row__n(decoder_4x16_1_out_8), .\input (\input ), .col__m(decoder_4x16_2_out_8),
    .reset(reset), .set__write_mode(set), .enable__read_mode(enable));  // open: output
  BYTE_REGISTER byte_register_152 (
    .contents(out_129), .row__n(decoder_4x16_1_out_9), .\input (\input ), .col__m(decoder_4x16_2_out_8),
    .reset(reset), .set__write_mode(set), .enable__read_mode(enable));  // open: output
  BYTE_REGISTER byte_register_153 (
    .contents(out_145), .row__n(decoder_4x16_1_out_10), .\input (\input ), .col__m(decoder_4x16_2_out_8),
    .reset(reset), .set__write_mode(set), .enable__read_mode(enable));  // open: output
  BYTE_REGISTER byte_register_154 (
    .contents(out_161), .row__n(decoder_4x16_1_out_11), .\input (\input ), .col__m(decoder_4x16_2_out_8),
    .reset(reset), .set__write_mode(set), .enable__read_mode(enable));  // open: output
  BYTE_REGISTER byte_register_155 (
    .contents(out_177), .row__n(decoder_4x16_1_out_12), .\input (\input ), .col__m(decoder_4x16_2_out_8),
    .reset(reset), .set__write_mode(set), .enable__read_mode(enable));  // open: output
  BYTE_REGISTER byte_register_156 (
    .contents(out_193), .row__n(decoder_4x16_1_out_13), .\input (\input ), .col__m(decoder_4x16_2_out_8),
    .reset(reset), .set__write_mode(set), .enable__read_mode(enable));  // open: output
  BYTE_REGISTER byte_register_157 (
    .contents(out_209), .row__n(decoder_4x16_1_out_14), .\input (\input ), .col__m(decoder_4x16_2_out_8),
    .reset(reset), .set__write_mode(set), .enable__read_mode(enable));  // open: output
  BYTE_REGISTER byte_register_158 (
    .contents(out_225), .row__n(decoder_4x16_1_out_15), .\input (\input ), .col__m(decoder_4x16_2_out_8),
    .reset(reset), .set__write_mode(set), .enable__read_mode(enable));  // open: output
  BYTE_REGISTER byte_register_159 (
    .contents(out_241), .row__n(decoder_4x16_1_out_16), .\input (\input ), .col__m(decoder_4x16_2_out_8),
    .reset(reset), .set__write_mode(set), .enable__read_mode(enable));  // open: output
  BYTE_REGISTER byte_register_160 (
    .contents(out_257), .row__n(decoder_4x16_1_msb), .\input (\input ), .col__m(decoder_4x16_2_out_8),
    .reset(reset), .set__write_mode(set), .enable__read_mode(enable));  // open: output
  BYTE_REGISTER byte_register_161 (
    .contents(out_18), .row__n(decoder_4x16_1_lsb), .\input (\input ), .col__m(decoder_4x16_2_out_7),
    .reset(reset), .set__write_mode(set), .enable__read_mode(enable), .\output (o));
  BYTE_REGISTER byte_register_162 (
    .contents(out_34), .row__n(decoder_4x16_1_out_3), .\input (\input ), .col__m(decoder_4x16_2_out_7),
    .reset(reset), .set__write_mode(set), .enable__read_mode(enable), .\output (o));
  BYTE_REGISTER byte_register_163 (
    .contents(out_50), .row__n(decoder_4x16_1_out_4), .\input (\input ), .col__m(decoder_4x16_2_out_7),
    .reset(reset), .set__write_mode(set), .enable__read_mode(enable), .\output (o));
  BYTE_REGISTER byte_register_164 (
    .contents(out_66), .row__n(decoder_4x16_1_out_5), .\input (\input ), .col__m(decoder_4x16_2_out_7),
    .reset(reset), .set__write_mode(set), .enable__read_mode(enable), .\output (o));
  BYTE_REGISTER byte_register_165 (
    .contents(out_82), .row__n(decoder_4x16_1_out_6), .\input (\input ), .col__m(decoder_4x16_2_out_7),
    .reset(reset), .set__write_mode(set), .enable__read_mode(enable), .\output (o));
  BYTE_REGISTER byte_register_166 (
    .contents(out_98), .row__n(decoder_4x16_1_out_7), .\input (\input ), .col__m(decoder_4x16_2_out_7),
    .reset(reset), .set__write_mode(set), .enable__read_mode(enable), .\output (o));
  BYTE_REGISTER byte_register_167 (
    .contents(out_114), .row__n(decoder_4x16_1_out_8), .\input (\input ), .col__m(decoder_4x16_2_out_7),
    .reset(reset), .set__write_mode(set), .enable__read_mode(enable), .\output (o));
  BYTE_REGISTER byte_register_168 (
    .contents(out_130), .row__n(decoder_4x16_1_out_9), .\input (\input ), .col__m(decoder_4x16_2_out_7),
    .reset(reset), .set__write_mode(set), .enable__read_mode(enable), .\output (o));
  BYTE_REGISTER byte_register_169 (
    .contents(out_146), .row__n(decoder_4x16_1_out_10), .\input (\input ), .col__m(decoder_4x16_2_out_7),
    .reset(reset), .set__write_mode(set), .enable__read_mode(enable), .\output (o));
  BYTE_REGISTER byte_register_170 (
    .contents(out_162), .row__n(decoder_4x16_1_out_11), .\input (\input ), .col__m(decoder_4x16_2_out_7),
    .reset(reset), .set__write_mode(set), .enable__read_mode(enable), .\output (o));
  BYTE_REGISTER byte_register_171 (
    .contents(out_178), .row__n(decoder_4x16_1_out_12), .\input (\input ), .col__m(decoder_4x16_2_out_7),
    .reset(reset), .set__write_mode(set), .enable__read_mode(enable), .\output (o));
  BYTE_REGISTER byte_register_172 (
    .contents(out_194), .row__n(decoder_4x16_1_out_13), .\input (\input ), .col__m(decoder_4x16_2_out_7),
    .reset(reset), .set__write_mode(set), .enable__read_mode(enable), .\output (o));
  BYTE_REGISTER byte_register_173 (
    .contents(out_210), .row__n(decoder_4x16_1_out_14), .\input (\input ), .col__m(decoder_4x16_2_out_7),
    .reset(reset), .set__write_mode(set), .enable__read_mode(enable), .\output (o));
  BYTE_REGISTER byte_register_174 (
    .contents(out_226), .row__n(decoder_4x16_1_out_15), .\input (\input ), .col__m(decoder_4x16_2_out_7),
    .reset(reset), .set__write_mode(set), .enable__read_mode(enable), .\output (o));
  BYTE_REGISTER byte_register_175 (
    .contents(out_242), .row__n(decoder_4x16_1_out_16), .\input (\input ), .col__m(decoder_4x16_2_out_7),
    .reset(reset), .set__write_mode(set), .enable__read_mode(enable), .\output (o));
  BYTE_REGISTER byte_register_176 (
    .contents(out_258), .row__n(decoder_4x16_1_msb), .\input (\input ), .col__m(decoder_4x16_2_out_7),
    .reset(reset), .set__write_mode(set), .enable__read_mode(enable), .\output (o));
  BYTE_REGISTER byte_register_177 (
    .contents(out_19), .row__n(decoder_4x16_1_lsb), .\input (\input ), .col__m(decoder_4x16_2_out_6),
    .reset(reset), .set__write_mode(set), .enable__read_mode(enable), .\output (o));
  BYTE_REGISTER byte_register_178 (
    .contents(out_35), .row__n(decoder_4x16_1_out_3), .\input (\input ), .col__m(decoder_4x16_2_out_6),
    .reset(reset), .set__write_mode(set), .enable__read_mode(enable), .\output (o));
  BYTE_REGISTER byte_register_179 (
    .contents(out_51), .row__n(decoder_4x16_1_out_4), .\input (\input ), .col__m(decoder_4x16_2_out_6),
    .reset(reset), .set__write_mode(set), .enable__read_mode(enable), .\output (o));
  BYTE_REGISTER byte_register_180 (
    .contents(out_67), .row__n(decoder_4x16_1_out_5), .\input (\input ), .col__m(decoder_4x16_2_out_6),
    .reset(reset), .set__write_mode(set), .enable__read_mode(enable), .\output (o));
  BYTE_REGISTER byte_register_181 (
    .contents(out_83), .row__n(decoder_4x16_1_out_6), .\input (\input ), .col__m(decoder_4x16_2_out_6),
    .reset(reset), .set__write_mode(set), .enable__read_mode(enable), .\output (o));
  BYTE_REGISTER byte_register_182 (
    .contents(out_99), .row__n(decoder_4x16_1_out_7), .\input (\input ), .col__m(decoder_4x16_2_out_6),
    .reset(reset), .set__write_mode(set), .enable__read_mode(enable), .\output (o));
  BYTE_REGISTER byte_register_183 (
    .contents(out_115), .row__n(decoder_4x16_1_out_8), .\input (\input ), .col__m(decoder_4x16_2_out_6),
    .reset(reset), .set__write_mode(set), .enable__read_mode(enable), .\output (o));
  BYTE_REGISTER byte_register_184 (
    .contents(out_131), .row__n(decoder_4x16_1_out_9), .\input (\input ), .col__m(decoder_4x16_2_out_6),
    .reset(reset), .set__write_mode(set), .enable__read_mode(enable), .\output (o));
  BYTE_REGISTER byte_register_185 (
    .contents(out_147), .row__n(decoder_4x16_1_out_10), .\input (\input ), .col__m(decoder_4x16_2_out_6),
    .reset(reset), .set__write_mode(set), .enable__read_mode(enable), .\output (o));
  BYTE_REGISTER byte_register_186 (
    .contents(out_163), .row__n(decoder_4x16_1_out_11), .\input (\input ), .col__m(decoder_4x16_2_out_6),
    .reset(reset), .set__write_mode(set), .enable__read_mode(enable), .\output (o));
  BYTE_REGISTER byte_register_187 (
    .contents(out_179), .row__n(decoder_4x16_1_out_12), .\input (\input ), .col__m(decoder_4x16_2_out_6),
    .reset(reset), .set__write_mode(set), .enable__read_mode(enable), .\output (o));
  BYTE_REGISTER byte_register_188 (
    .contents(out_195), .row__n(decoder_4x16_1_out_13), .\input (\input ), .col__m(decoder_4x16_2_out_6),
    .reset(reset), .set__write_mode(set), .enable__read_mode(enable), .\output (o));
  BYTE_REGISTER byte_register_189 (
    .contents(out_211), .row__n(decoder_4x16_1_out_14), .\input (\input ), .col__m(decoder_4x16_2_out_6),
    .reset(reset), .set__write_mode(set), .enable__read_mode(enable), .\output (o));
  BYTE_REGISTER byte_register_190 (
    .contents(out_227), .row__n(decoder_4x16_1_out_15), .\input (\input ), .col__m(decoder_4x16_2_out_6),
    .reset(reset), .set__write_mode(set), .enable__read_mode(enable), .\output (o));
  BYTE_REGISTER byte_register_191 (
    .contents(out_243), .row__n(decoder_4x16_1_out_16), .\input (\input ), .col__m(decoder_4x16_2_out_6),
    .reset(reset), .set__write_mode(set), .enable__read_mode(enable), .\output (o));
  BYTE_REGISTER byte_register_192 (
    .contents(out_259), .row__n(decoder_4x16_1_msb), .\input (\input ), .col__m(decoder_4x16_2_out_6),
    .reset(reset), .set__write_mode(set), .enable__read_mode(enable), .\output (o));
  BYTE_REGISTER byte_register_193 (
    .contents(out_20), .row__n(decoder_4x16_1_lsb), .\input (\input ), .col__m(decoder_4x16_2_out_5),
    .reset(reset), .set__write_mode(set), .enable__read_mode(enable), .\output (o));
  BYTE_REGISTER byte_register_194 (
    .contents(out_36), .row__n(decoder_4x16_1_out_3), .\input (\input ), .col__m(decoder_4x16_2_out_5),
    .reset(reset), .set__write_mode(set), .enable__read_mode(enable), .\output (o));
  BYTE_REGISTER byte_register_195 (
    .contents(out_52), .row__n(decoder_4x16_1_out_4), .\input (\input ), .col__m(decoder_4x16_2_out_5),
    .reset(reset), .set__write_mode(set), .enable__read_mode(enable), .\output (o));
  BYTE_REGISTER byte_register_196 (
    .contents(out_68), .row__n(decoder_4x16_1_out_5), .\input (\input ), .col__m(decoder_4x16_2_out_5),
    .reset(reset), .set__write_mode(set), .enable__read_mode(enable), .\output (o));
  BYTE_REGISTER byte_register_197 (
    .contents(out_84), .row__n(decoder_4x16_1_out_6), .\input (\input ), .col__m(decoder_4x16_2_out_5),
    .reset(reset), .set__write_mode(set), .enable__read_mode(enable), .\output (o));
  BYTE_REGISTER byte_register_198 (
    .contents(out_100), .row__n(decoder_4x16_1_out_7), .\input (\input ), .col__m(decoder_4x16_2_out_5),
    .reset(reset), .set__write_mode(set), .enable__read_mode(enable), .\output (o));
  BYTE_REGISTER byte_register_199 (
    .contents(out_116), .row__n(decoder_4x16_1_out_8), .\input (\input ), .col__m(decoder_4x16_2_out_5),
    .reset(reset), .set__write_mode(set), .enable__read_mode(enable), .\output (o));
  BYTE_REGISTER byte_register_200 (
    .contents(out_132), .row__n(decoder_4x16_1_out_9), .\input (\input ), .col__m(decoder_4x16_2_out_5),
    .reset(reset), .set__write_mode(set), .enable__read_mode(enable), .\output (o));
  BYTE_REGISTER byte_register_201 (
    .contents(out_148), .row__n(decoder_4x16_1_out_10), .\input (\input ), .col__m(decoder_4x16_2_out_5),
    .reset(reset), .set__write_mode(set), .enable__read_mode(enable), .\output (o));
  BYTE_REGISTER byte_register_202 (
    .contents(out_164), .row__n(decoder_4x16_1_out_11), .\input (\input ), .col__m(decoder_4x16_2_out_5),
    .reset(reset), .set__write_mode(set), .enable__read_mode(enable), .\output (o));
  BYTE_REGISTER byte_register_203 (
    .contents(out_180), .row__n(decoder_4x16_1_out_12), .\input (\input ), .col__m(decoder_4x16_2_out_5),
    .reset(reset), .set__write_mode(set), .enable__read_mode(enable), .\output (o));
  BYTE_REGISTER byte_register_204 (
    .contents(out_196), .row__n(decoder_4x16_1_out_13), .\input (\input ), .col__m(decoder_4x16_2_out_5),
    .reset(reset), .set__write_mode(set), .enable__read_mode(enable), .\output (o));
  BYTE_REGISTER byte_register_205 (
    .contents(out_212), .row__n(decoder_4x16_1_out_14), .\input (\input ), .col__m(decoder_4x16_2_out_5),
    .reset(reset), .set__write_mode(set), .enable__read_mode(enable), .\output (o));
  BYTE_REGISTER byte_register_206 (
    .contents(out_228), .row__n(decoder_4x16_1_out_15), .\input (\input ), .col__m(decoder_4x16_2_out_5),
    .reset(reset), .set__write_mode(set), .enable__read_mode(enable), .\output (o));
  BYTE_REGISTER byte_register_207 (
    .contents(out_244), .row__n(decoder_4x16_1_out_16), .\input (\input ), .col__m(decoder_4x16_2_out_5),
    .reset(reset), .set__write_mode(set), .enable__read_mode(enable), .\output (o));
  BYTE_REGISTER byte_register_208 (
    .contents(out_260), .row__n(decoder_4x16_1_msb), .\input (\input ), .col__m(decoder_4x16_2_out_5),
    .reset(reset), .set__write_mode(set), .enable__read_mode(enable), .\output (o));
  BYTE_REGISTER byte_register_209 (
    .contents(out_21), .row__n(decoder_4x16_1_lsb), .\input (\input ), .col__m(decoder_4x16_2_out_4),
    .reset(reset), .set__write_mode(set), .enable__read_mode(enable), .\output (o));
  BYTE_REGISTER byte_register_210 (
    .contents(out_37), .row__n(decoder_4x16_1_out_3), .col__m(decoder_4x16_2_out_4), .reset(reset),
    .set__write_mode(set), .enable__read_mode(enable), .\output (o));  // open: input
  BYTE_REGISTER byte_register_211 (
    .contents(out_53), .row__n(decoder_4x16_1_out_4), .\input (\input ), .col__m(decoder_4x16_2_out_4),
    .reset(reset), .set__write_mode(set), .enable__read_mode(enable), .\output (o));
  BYTE_REGISTER byte_register_212 (
    .contents(out_69), .row__n(decoder_4x16_1_out_5), .\input (\input ), .col__m(decoder_4x16_2_out_4),
    .reset(reset), .set__write_mode(set), .enable__read_mode(enable), .\output (o));
  BYTE_REGISTER byte_register_213 (
    .contents(out_85), .row__n(decoder_4x16_1_out_6), .\input (\input ), .col__m(decoder_4x16_2_out_4),
    .reset(reset), .set__write_mode(set), .enable__read_mode(enable), .\output (o));
  BYTE_REGISTER byte_register_214 (
    .contents(out_101), .row__n(decoder_4x16_1_out_7), .\input (\input ), .col__m(decoder_4x16_2_out_4),
    .reset(reset), .set__write_mode(set), .enable__read_mode(enable), .\output (o));
  BYTE_REGISTER byte_register_215 (
    .contents(out_117), .row__n(decoder_4x16_1_out_8), .\input (\input ), .col__m(decoder_4x16_2_out_4),
    .reset(reset), .set__write_mode(set), .enable__read_mode(enable), .\output (o));
  BYTE_REGISTER byte_register_216 (
    .contents(out_133), .row__n(decoder_4x16_1_out_9), .\input (\input ), .col__m(decoder_4x16_2_out_4),
    .reset(reset), .set__write_mode(set), .enable__read_mode(enable), .\output (o));
  BYTE_REGISTER byte_register_217 (
    .contents(out_149), .row__n(decoder_4x16_1_out_10), .\input (\input ), .col__m(decoder_4x16_2_out_4),
    .reset(reset), .set__write_mode(set), .enable__read_mode(enable), .\output (o));
  BYTE_REGISTER byte_register_218 (
    .contents(out_165), .row__n(decoder_4x16_1_out_11), .\input (\input ), .col__m(decoder_4x16_2_out_4),
    .reset(reset), .set__write_mode(set), .enable__read_mode(enable), .\output (o));
  BYTE_REGISTER byte_register_219 (
    .contents(out_181), .row__n(decoder_4x16_1_out_12), .\input (\input ), .col__m(decoder_4x16_2_out_4),
    .reset(reset), .set__write_mode(set), .enable__read_mode(enable), .\output (o));
  BYTE_REGISTER byte_register_220 (
    .contents(out_197), .row__n(decoder_4x16_1_out_13), .\input (\input ), .col__m(decoder_4x16_2_out_4),
    .reset(reset), .set__write_mode(set), .enable__read_mode(enable), .\output (o));
  BYTE_REGISTER byte_register_221 (
    .contents(out_213), .row__n(decoder_4x16_1_out_14), .\input (\input ), .col__m(decoder_4x16_2_out_4),
    .reset(reset), .set__write_mode(set), .enable__read_mode(enable), .\output (o));
  BYTE_REGISTER byte_register_222 (
    .contents(out_229), .row__n(decoder_4x16_1_out_15), .\input (\input ), .col__m(decoder_4x16_2_out_4),
    .reset(reset), .set__write_mode(set), .enable__read_mode(enable), .\output (o));
  BYTE_REGISTER byte_register_223 (
    .contents(out_245), .row__n(decoder_4x16_1_out_16), .\input (\input ), .col__m(decoder_4x16_2_out_4),
    .reset(reset), .set__write_mode(set), .enable__read_mode(enable), .\output (o));
  BYTE_REGISTER byte_register_224 (
    .contents(out_261), .row__n(decoder_4x16_1_msb), .\input (\input ), .col__m(decoder_4x16_2_out_4),
    .reset(reset), .set__write_mode(set), .enable__read_mode(enable), .\output (o));
  BYTE_REGISTER byte_register_225 (
    .contents(out_22), .row__n(decoder_4x16_1_lsb), .\input (\input ), .col__m(decoder_4x16_2_out_3),
    .reset(reset), .set__write_mode(set), .enable__read_mode(enable), .\output (o));
  BYTE_REGISTER byte_register_226 (
    .contents(out_38), .row__n(decoder_4x16_1_out_3), .\input (\input ), .col__m(decoder_4x16_2_out_3),
    .set__write_mode(set), .enable__read_mode(enable), .\output (o));  // open: reset
  BYTE_REGISTER byte_register_227 (
    .contents(out_54), .row__n(decoder_4x16_1_out_4), .\input (\input ), .col__m(decoder_4x16_2_out_3),
    .reset(reset), .set__write_mode(set), .enable__read_mode(enable), .\output (o));
  BYTE_REGISTER byte_register_228 (
    .contents(out_70), .row__n(decoder_4x16_1_out_5), .\input (\input ), .col__m(decoder_4x16_2_out_3),
    .reset(reset), .set__write_mode(set), .enable__read_mode(enable), .\output (o));
  BYTE_REGISTER byte_register_229 (
    .contents(out_86), .row__n(decoder_4x16_1_out_6), .\input (\input ), .col__m(decoder_4x16_2_out_3),
    .reset(reset), .set__write_mode(set), .enable__read_mode(enable), .\output (o));
  BYTE_REGISTER byte_register_230 (
    .contents(out_102), .row__n(decoder_4x16_1_out_7), .\input (\input ), .col__m(decoder_4x16_2_out_3),
    .reset(reset), .set__write_mode(set), .enable__read_mode(enable), .\output (o));
  BYTE_REGISTER byte_register_231 (
    .contents(out_118), .row__n(decoder_4x16_1_out_8), .\input (\input ), .col__m(decoder_4x16_2_out_3),
    .reset(reset), .set__write_mode(set), .enable__read_mode(enable), .\output (o));
  BYTE_REGISTER byte_register_232 (
    .contents(out_134), .row__n(decoder_4x16_1_out_9), .\input (\input ), .col__m(decoder_4x16_2_out_3),
    .reset(reset), .set__write_mode(set), .enable__read_mode(enable), .\output (o));
  BYTE_REGISTER byte_register_233 (
    .contents(out_150), .row__n(decoder_4x16_1_out_10), .\input (\input ), .col__m(decoder_4x16_2_out_3),
    .reset(reset), .set__write_mode(set), .enable__read_mode(enable), .\output (o));
  BYTE_REGISTER byte_register_234 (
    .contents(out_166), .row__n(decoder_4x16_1_out_11), .\input (\input ), .col__m(decoder_4x16_2_out_3),
    .reset(reset), .set__write_mode(set), .enable__read_mode(enable), .\output (o));
  BYTE_REGISTER byte_register_235 (
    .contents(out_182), .row__n(decoder_4x16_1_out_12), .\input (\input ), .col__m(decoder_4x16_2_out_3),
    .reset(reset), .set__write_mode(set), .enable__read_mode(enable), .\output (o));
  BYTE_REGISTER byte_register_236 (
    .contents(out_198), .row__n(decoder_4x16_1_out_13), .\input (\input ), .col__m(decoder_4x16_2_out_3),
    .reset(reset), .set__write_mode(set), .enable__read_mode(enable), .\output (o));
  // BYTE_REGISTER byte_register_237: pin names not known; wires that end beside it: decoder_4x16_1_out_14, \input , decoder_4x16_2_out_3, set, out_214, enable, reset, o
  BYTE_REGISTER byte_register_238 (
    .contents(out_230), .row__n(decoder_4x16_1_out_15), .\input (\input ), .col__m(decoder_4x16_2_out_3),
    .reset(reset), .set__write_mode(set), .enable__read_mode(enable), .\output (o));
  BYTE_REGISTER byte_register_239 (
    .contents(out_246), .row__n(decoder_4x16_1_out_16), .\input (\input ), .col__m(decoder_4x16_2_out_3),
    .reset(reset), .set__write_mode(set), .enable__read_mode(enable), .\output (o));
  BYTE_REGISTER byte_register_240 (
    .contents(out_262), .row__n(decoder_4x16_1_msb), .\input (\input ), .col__m(decoder_4x16_2_out_3),
    .reset(reset), .set__write_mode(set), .enable__read_mode(enable), .\output (o));
  BYTE_REGISTER byte_register_241 (
    .contents(out_23), .row__n(decoder_4x16_1_lsb), .\input (\input ), .col__m(decoder_4x16_2_lsb),
    .reset(reset), .set__write_mode(set), .enable__read_mode(enable), .\output (o));
  BYTE_REGISTER byte_register_242 (
    .contents(out_39), .row__n(decoder_4x16_1_out_3), .\input (\input ), .col__m(decoder_4x16_2_lsb),
    .reset(reset), .set__write_mode(set), .enable__read_mode(enable), .\output (o));
  BYTE_REGISTER byte_register_243 (
    .contents(out_55), .row__n(decoder_4x16_1_out_4), .\input (\input ), .col__m(decoder_4x16_2_lsb),
    .reset(reset), .set__write_mode(set), .enable__read_mode(enable), .\output (o));
  BYTE_REGISTER byte_register_244 (
    .contents(out_71), .row__n(decoder_4x16_1_out_5), .\input (\input ), .col__m(decoder_4x16_2_lsb),
    .reset(reset), .set__write_mode(set), .enable__read_mode(enable), .\output (o));
  BYTE_REGISTER byte_register_245 (
    .contents(out_87), .row__n(decoder_4x16_1_out_6), .\input (\input ), .col__m(decoder_4x16_2_lsb),
    .reset(reset), .set__write_mode(set), .enable__read_mode(enable), .\output (o));
  BYTE_REGISTER byte_register_246 (
    .contents(out_103), .row__n(decoder_4x16_1_out_7), .\input (\input ), .col__m(decoder_4x16_2_lsb),
    .reset(reset), .set__write_mode(set), .enable__read_mode(enable), .\output (o));
  BYTE_REGISTER byte_register_247 (
    .contents(out_119), .row__n(decoder_4x16_1_out_8), .\input (\input ), .col__m(decoder_4x16_2_lsb),
    .reset(reset), .set__write_mode(set), .enable__read_mode(enable), .\output (o));
  BYTE_REGISTER byte_register_248 (
    .contents(out_135), .row__n(decoder_4x16_1_out_9), .\input (\input ), .col__m(decoder_4x16_2_lsb),
    .reset(reset), .set__write_mode(set), .enable__read_mode(enable), .\output (o));
  BYTE_REGISTER byte_register_249 (
    .contents(out_151), .row__n(decoder_4x16_1_out_10), .\input (\input ), .col__m(decoder_4x16_2_lsb),
    .reset(reset), .set__write_mode(set), .enable__read_mode(enable), .\output (o));
  BYTE_REGISTER byte_register_250 (
    .contents(out_167), .row__n(decoder_4x16_1_out_11), .\input (\input ), .col__m(decoder_4x16_2_lsb),
    .reset(reset), .set__write_mode(set), .enable__read_mode(enable), .\output (o));
  BYTE_REGISTER byte_register_251 (
    .contents(out_183), .row__n(decoder_4x16_1_out_12), .\input (\input ), .col__m(decoder_4x16_2_lsb),
    .reset(reset), .set__write_mode(set), .enable__read_mode(enable), .\output (o));
  BYTE_REGISTER byte_register_252 (
    .contents(out_199), .row__n(decoder_4x16_1_out_13), .\input (\input ), .col__m(decoder_4x16_2_lsb),
    .reset(reset), .set__write_mode(set), .enable__read_mode(enable), .\output (o));
  BYTE_REGISTER byte_register_253 (
    .contents(out_215), .row__n(decoder_4x16_1_out_14), .\input (\input ), .col__m(decoder_4x16_2_lsb),
    .reset(reset), .set__write_mode(set), .enable__read_mode(enable), .\output (o));
  BYTE_REGISTER byte_register_254 (
    .contents(out_231), .row__n(decoder_4x16_1_out_15), .\input (\input ), .col__m(decoder_4x16_2_lsb),
    .reset(reset), .set__write_mode(set), .enable__read_mode(enable), .\output (o));
  BYTE_REGISTER byte_register_255 (
    .contents(out_247), .row__n(decoder_4x16_1_out_16), .\input (\input ), .col__m(decoder_4x16_2_lsb),
    .reset(reset), .set__write_mode(set), .enable__read_mode(enable), .\output (o));
  BYTE_REGISTER byte_register_256 (
    .contents(out_263), .row__n(decoder_4x16_1_msb), .\input (\input ), .col__m(decoder_4x16_2_lsb),
    .reset(reset), .set__write_mode(set), .enable__read_mode(enable), .\output (o));

  // Other names for the same wires on the sheet: e = enable; i[7:0] = \input ; s = set
endmodule

module FULL_ADDER_1 (
  input  a,
  input  b,
  input  carry_in,
  output sum,
  output carry_out
);

  wire and_1_out, and_2_out, sum_1;

  xor xor_1 (sum_1, a, b);
  and and_1 (and_1_out, carry_in, sum_1);
  and and_2 (and_2_out, a, b);
  xor xor_2 (sum, sum_1, carry_in);
  or or_1 (carry_out, and_1_out, and_2_out);
endmodule

module FULL_ADDER_8 (
  input  [7:0] a,
  input  [7:0] b,
  input  carry_in,
  output carry_out,
  output [7:0] sum
);

  wire full_adder_1_2_carry_out, full_adder_1_3_carry_out, full_adder_1_4_carry_out,
       full_adder_1_5_carry_out, full_adder_1_6_carry_out, full_adder_1_7_carry_out, full_adder_1_8_carry_out;

  FULL_ADDER_1 full_adder_1_1 (
    .a(a[7]), .b(b[7]), .carry_in(full_adder_1_2_carry_out), .sum(sum[7]), .carry_out(carry_out));
  FULL_ADDER_1 full_adder_1_2 (
    .a(a[6]), .b(b[6]), .carry_in(full_adder_1_3_carry_out), .sum(sum[6]),
    .carry_out(full_adder_1_2_carry_out));
  FULL_ADDER_1 full_adder_1_3 (
    .a(a[5]), .b(b[5]), .carry_in(full_adder_1_4_carry_out), .sum(sum[5]),
    .carry_out(full_adder_1_3_carry_out));
  FULL_ADDER_1 full_adder_1_4 (
    .a(a[4]), .b(b[4]), .carry_in(full_adder_1_5_carry_out), .sum(sum[4]),
    .carry_out(full_adder_1_4_carry_out));
  FULL_ADDER_1 full_adder_1_5 (
    .a(a[3]), .b(b[3]), .carry_in(full_adder_1_6_carry_out), .sum(sum[3]),
    .carry_out(full_adder_1_5_carry_out));
  FULL_ADDER_1 full_adder_1_6 (
    .a(a[2]), .b(b[2]), .carry_in(full_adder_1_7_carry_out), .sum(sum[2]),
    .carry_out(full_adder_1_6_carry_out));
  FULL_ADDER_1 full_adder_1_7 (
    .a(a[1]), .b(b[1]), .carry_in(full_adder_1_8_carry_out), .sum(sum[1]),
    .carry_out(full_adder_1_7_carry_out));
  FULL_ADDER_1 full_adder_1_8 (
    .a(a[0]), .b(b[0]), .carry_in(carry_in), .sum(sum[0]), .carry_out(full_adder_1_8_carry_out));
endmodule

module SHIFT_RIGHT (
  input  [7:0] \input ,
  input  shift_in,
  output shift_out,
  output [7:0] \output 
);

  wire [7:1] register_1_output__read__bits;

  REGISTER register_1 (
    .input__write__data(\input ), .enable(1'b1),
    .output__read__bits({register_1_output__read__bits, shift_out}), .set_bit(1'b1));  // open: current_register_data
  REGISTER register_2 (
    .input__write__data({shift_in, register_1_output__read__bits}), .enable(1'b1),
    .output__read__bits(\output ), .set_bit(1'b1));  // open: current_register_data
endmodule

module SHIFT_LEFT (
  input  shift_in,
  input  [7:0] \input ,
  output [7:0] \output ,
  output shift_out
);

  wire [6:0] register_1_output__read__bits;

  REGISTER register_1 (
    .input__write__data(\input ), .enable(1'b1),
    .output__read__bits({shift_out, register_1_output__read__bits}), .set_bit(1'b1));  // open: current_register_data
  REGISTER register_2 (
    .input__write__data({register_1_output__read__bits, shift_in}), .enable(1'b1),
    .output__read__bits(\output ), .set_bit(1'b1));  // open: current_register_data
endmodule

module ALU_NOT (
  input  [7:0] \input ,
  output [7:0] \output 
);

  not not_1 (\output [0], \input [0]);
  not not_2 (\output [1], \input [1]);
  not not_3 (\output [2], \input [2]);
  not not_4 (\output [3], \input [3]);
  not not_5 (\output [4], \input [4]);
  not not_6 (\output [5], \input [5]);
  not not_7 (\output [6], \input [6]);
  not not_8 (\output [7], \input [7]);
endmodule

module ALU_OR (
  input  [7:0] a,
  input  [7:0] b,
  output [7:0] \output 
);

  or or_1 (\output [0], a[0], b[0]);
  or or_2 (\output [1], a[1], b[1]);
  or or_3 (\output [2], a[2], b[2]);
  or or_4 (\output [3], a[3], b[3]);
  or or_5 (\output [4], a[4], b[4]);
  or or_6 (\output [5], a[5], b[5]);
  or or_7 (\output [6], a[6], b[6]);
  or or_8 (\output [7], a[7], b[7]);
endmodule

module ALU_AND (
  input  [7:0] a,
  input  [7:0] b,
  output [7:0] \output 
);

  and and_1 (\output [0], a[0], b[0]);
  and and_2 (\output [1], a[1], b[1]);
  and and_3 (\output [2], a[2], b[2]);
  and and_4 (\output [3], a[3], b[3]);
  and and_5 (\output [4], a[4], b[4]);
  and and_6 (\output [5], a[5], b[5]);
  and and_7 (\output [6], a[6], b[6]);
  and and_8 (\output [7], a[7], b[7]);
endmodule

module XOR_1 (
  input  above_equal,
  input  a_larger,
  input  a,
  input  b,
  output \output ,
  output equal,
  output a_large
);

  wire and_2_out, not_1_out;

  xor xor_1 (\output , a, b);
  not not_1 (not_1_out, \output );
  and and_1 (equal, not_1_out, above_equal);
  and and_2 (and_2_out, above_equal, a, \output );
  or or_1 (a_large, and_2_out, a_larger);
endmodule

module ALU_XOR (
  input  [7:0] a,
  input  [7:0] b,
  output [7:0] \output ,
  output equal,
  output larger
);

  wire xor_1_1_a_large, xor_1_1_equal, xor_1_2_a_large, xor_1_2_equal, xor_1_3_a_large, xor_1_3_equal,
       xor_1_4_a_large, xor_1_4_equal, xor_1_5_a_large, xor_1_5_equal, xor_1_6_a_large, xor_1_6_equal,
       xor_1_7_a_large, xor_1_7_equal;

  XOR_1 xor_1_1 (
    .a(a[7]), .b(b[7]), .above_equal(1'b1), .a_larger(1'b0), .\output (\output [7]), .equal(xor_1_1_equal),
    .a_large(xor_1_1_a_large));
  XOR_1 xor_1_2 (
    .a(a[6]), .b(b[6]), .above_equal(xor_1_1_equal), .a_larger(xor_1_1_a_large), .\output (\output [6]),
    .equal(xor_1_2_equal), .a_large(xor_1_2_a_large));
  XOR_1 xor_1_3 (
    .a(a[5]), .b(b[5]), .above_equal(xor_1_2_equal), .a_larger(xor_1_2_a_large), .\output (\output [5]),
    .equal(xor_1_3_equal), .a_large(xor_1_3_a_large));
  XOR_1 xor_1_4 (
    .a(a[4]), .b(b[4]), .above_equal(xor_1_3_equal), .a_larger(xor_1_3_a_large), .\output (\output [4]),
    .equal(xor_1_4_equal), .a_large(xor_1_4_a_large));
  XOR_1 xor_1_5 (
    .a(a[3]), .b(b[3]), .above_equal(xor_1_4_equal), .a_larger(xor_1_4_a_large), .\output (\output [3]),
    .equal(xor_1_5_equal), .a_large(xor_1_5_a_large));
  XOR_1 xor_1_6 (
    .a(a[2]), .b(b[2]), .above_equal(xor_1_5_equal), .a_larger(xor_1_5_a_large), .\output (\output [2]),
    .equal(xor_1_6_equal), .a_large(xor_1_6_a_large));
  XOR_1 xor_1_7 (
    .a(a[1]), .b(b[1]), .above_equal(xor_1_6_equal), .a_larger(xor_1_6_a_large), .\output (\output [1]),
    .equal(xor_1_7_equal), .a_large(xor_1_7_a_large));
  XOR_1 xor_1_8 (
    .a(a[0]), .b(b[0]), .above_equal(xor_1_7_equal), .a_larger(xor_1_7_a_large), .\output (\output [0]),
    .equal(equal), .a_large(larger));
endmodule

module ZERO (
  input  [7:0] \input ,
  output \output 
);

  wire or_1_out;

  or or_1 (or_1_out, \input [0], \input [1], \input [2], \input [3], \input [4], \input [5], \input [6], \input [7]);
  not not_1 (\output , or_1_out);
endmodule

module ENABLER (
  input  [7:0] in_1,
  input  in_2,
  output [7:0] out_3
);

  wire and_1_out, and_2_out, and_3_out, and_4_out, and_5_out, and_6_out, and_7_out, and_8_out;

  assign out_3[0] = in_2 ? and_1_out : 1'bz;  // Controlled_Buffer controlled_buffer_1
  and and_1 (and_1_out, in_1[0], in_2);
  and and_2 (and_2_out, in_1[1], in_2);
  assign out_3[1] = in_2 ? and_2_out : 1'bz;  // Controlled_Buffer controlled_buffer_2
  and and_3 (and_3_out, in_1[2], in_2);
  assign out_3[2] = in_2 ? and_3_out : 1'bz;  // Controlled_Buffer controlled_buffer_3
  assign out_3[3] = in_2 ? and_4_out : 1'bz;  // Controlled_Buffer controlled_buffer_4
  and and_4 (and_4_out, in_1[3], in_2);
  assign out_3[4] = in_2 ? and_5_out : 1'bz;  // Controlled_Buffer controlled_buffer_5
  and and_5 (and_5_out, in_1[4], in_2);
  assign out_3[5] = in_2 ? and_6_out : 1'bz;  // Controlled_Buffer controlled_buffer_6
  and and_6 (and_6_out, in_1[5], in_2);
  and and_7 (and_7_out, in_1[6], in_2);
  assign out_3[6] = in_2 ? and_7_out : 1'bz;  // Controlled_Buffer controlled_buffer_7
  assign out_3[7] = in_2 ? and_8_out : 1'bz;  // Controlled_Buffer controlled_buffer_8
  and and_8 (and_8_out, in_1[7], in_2);
endmodule

module ARITHMETIC_LOGIC_UNIT (
  input  [7:0] a,
  input  [7:0] b,
  input  carry_in,
  input  a_2,
  input  b_2,
  input  c,
  output a_larger,
  output equal,
  output zero,
  output [7:0] \output ,
  output carry_out
);

  wire and_1_out, and_2_out, and_3_out, full_adder_8_1_carry_out, shift_left_1_shift_out,
       shift_right_1_shift_out;
  wire [7:0] alu_and_1_output, alu_not_1_output, alu_or_1_output, alu_xor_1_output, decoder_3x8_1_out_4,
       full_adder_8_1_sum, shift_left_1_output, shift_right_1_output;

  ALU_XOR alu_xor_1 (.a(a), .b(b), .\output (alu_xor_1_output), .equal(equal), .larger(a_larger));
  ALU_OR alu_or_1 (.a(a), .b(b), .\output (alu_or_1_output));
  ALU_AND alu_and_1 (.a(a), .b(b), .\output (alu_and_1_output));
  ALU_NOT alu_not_1 (.\input (a), .\output (alu_not_1_output));
  SHIFT_LEFT shift_left_1 (
    .\input (a), .\output (shift_left_1_output), .shift_in(carry_in), .shift_out(shift_left_1_shift_out));
  SHIFT_RIGHT shift_right_1 (
    .\input (a), .\output (shift_right_1_output), .shift_out(shift_right_1_shift_out), .shift_in(carry_in));
  FULL_ADDER_8 full_adder_8_1 (
    .a(a), .b(b), .sum(full_adder_8_1_sum), .carry_out(full_adder_8_1_carry_out), .carry_in(carry_in));
  DECODER_3x8 decoder_3x8_1 (.out_4(decoder_3x8_1_out_4), .MSB(a_2), .middle(b_2), .LSB(c));
  ENABLER enabler_1 (.in_1(alu_xor_1_output), .out_3(\output ), .in_2(decoder_3x8_1_out_4[6]));
  ENABLER enabler_2 (.in_1(alu_or_1_output), .out_3(\output ), .in_2(decoder_3x8_1_out_4[5]));
  ENABLER enabler_3 (.in_1(alu_and_1_output), .out_3(\output ), .in_2(decoder_3x8_1_out_4[4]));
  ENABLER enabler_4 (.in_1(alu_not_1_output), .out_3(\output ), .in_2(decoder_3x8_1_out_4[3]));
  ENABLER enabler_5 (.in_1(shift_left_1_output), .out_3(\output ), .in_2(decoder_3x8_1_out_4[2]));
  ENABLER enabler_6 (.in_1(shift_right_1_output), .out_3(\output ), .in_2(decoder_3x8_1_out_4[1]));
  ENABLER enabler_7 (.in_1(full_adder_8_1_sum), .out_3(\output ), .in_2(decoder_3x8_1_out_4[0]));
  and and_1 (and_1_out, decoder_3x8_1_out_4[2], shift_left_1_shift_out);
  and and_2 (and_2_out, decoder_3x8_1_out_4[1], shift_right_1_shift_out);
  assign carry_out = decoder_3x8_1_out_4[2] ? and_1_out : 1'bz;  // Controlled_Buffer controlled_buffer_1
  and and_3 (and_3_out, decoder_3x8_1_out_4[0], full_adder_8_1_carry_out);
  assign carry_out = decoder_3x8_1_out_4[1] ? ~and_2_out : 1'bz;  // Controlled_Inverter controlled_inverter_1
  assign carry_out = decoder_3x8_1_out_4[0] ? and_3_out : 1'bz;  // Controlled_Buffer controlled_buffer_2
  ZERO zero_1 (.\input (\output ), .\output (zero));
endmodule

module INTERNAL_CLOCK (
  input  clkin,
  output clk,
  output clks,
  output clke
);

  wire j_k_ff_1_qn, nand_1_out;

  J_K_Flip_Flop j_k_ff_1 (.J(1'b1), .clk(clkin), .K(1'b1), .Q(clk), .Qn(j_k_ff_1_qn));  // open: preset, en, reset
  nand nand_1 (nand_1_out, clkin, clk);
  nand nand_2 (clke, j_k_ff_1_qn, clkin);
  not not_1 (clks, nand_1_out);

  // Notes on the sheet:
  //   clkin: pull=down
  //   clks: pull=down
  //   clk: pull=down
  //   clke: pull=down
endmodule

module BUS (
  input  [7:0] i,
  input  bus_1,
  output [7:0] o
);

  wire not_1_out;

  and and_1 (o[7], i[7], not_1_out);
  and and_2 (o[6], i[6], not_1_out);
  and and_3 (o[5], i[5], not_1_out);
  and and_4 (o[4], i[4], not_1_out);
  and and_5 (o[3], i[3], not_1_out);
  and and_6 (o[2], i[2], not_1_out);
  and and_7 (o[1], i[1], not_1_out);
  not not_1 (not_1_out, bus_1);
  or or_1 (o[0], i[0], bus_1);

  // Notes on the sheet:
  //   bus_1: pull=down
  //   o: pull=down
  //   i: pull=down
endmodule

module ACCUMULATOR (
  input  [7:0] i,
  input  s,
  input  e,
  output [7:0] ACC,
  output [7:0] o
);

  // REGISTER register_1: pin names not known; wires that end beside it: ACC, i, s, e, o

  // Notes on the sheet:
  //   i: pull=down
  //   s: pull=down
  //   o: pull=down
  //   e: pull=down
endmodule

module TEMP (
  input  [7:0] i,
  input  s,
  output [7:0] o
);

  wire [7:0] controlled_buffer_1_out;

  assign controlled_buffer_1_out = s ? i : 8'bz;  // Controlled_Buffer controlled_buffer_1
  MEM_8 mem_8_1 (.\input (controlled_buffer_1_out), .out_3(o), .set(s));

  // Notes on the sheet:
  //   i: pull=down
  //   s: pull=down
  //   o: pull=down
endmodule

module STEPPER (
  input  reset,
  input  clk,
  output step_1,
  output step_2,
  output step_3,
  output step_4,
  output step_5,
  output step_6,
  output step_7
);

  wire mem_1_1_q, mem_1_2_q, mem_1_3_q, mem_1_4_q, mem_1_5_q, mem_1_6_q, mem_1_7_q, mem_1_8_q, mem_1_9_q,
       mem_1_10_q, mem_1_11_q, not_1_out, not_2_out, not_3_out, not_4_out, not_5_out, not_6_out, not_7_out,
       not_8_out, or_1_out, or_2_out;

  not not_1 (not_1_out, clk);
  not not_2 (not_2_out, reset);
  or or_1 (or_1_out, reset, clk);
  or or_2 (or_2_out, reset, not_1_out);
  or or_3 (step_1, reset, not_3_out);
  MEM_1 mem_1_1 (.s(not_2_out), .E(or_1_out), .Q(mem_1_1_q));
  not not_3 (not_3_out, mem_1_2_q);
  MEM_1 mem_1_2 (.s(mem_1_1_q), .E(or_2_out), .Q(mem_1_2_q));
  and and_1 (step_2, mem_1_2_q, not_4_out);
  not not_4 (not_4_out, mem_1_4_q);
  MEM_1 mem_1_3 (.s(mem_1_2_q), .E(or_1_out), .Q(mem_1_3_q));
  MEM_1 mem_1_4 (.s(mem_1_3_q), .E(or_2_out), .Q(mem_1_4_q));
  and and_2 (step_3, mem_1_4_q, not_5_out);
  MEM_1 mem_1_5 (.s(mem_1_4_q), .E(or_1_out), .Q(mem_1_5_q));
  not not_5 (not_5_out, mem_1_6_q);
  MEM_1 mem_1_6 (.s(mem_1_5_q), .E(or_2_out), .Q(mem_1_6_q));
  and and_3 (step_4, mem_1_6_q, not_6_out);
  not not_6 (not_6_out, mem_1_8_q);
  MEM_1 mem_1_7 (.s(mem_1_6_q), .E(or_1_out), .Q(mem_1_7_q));
  and and_4 (step_5, mem_1_8_q, not_7_out);
  MEM_1 mem_1_8 (.s(mem_1_7_q), .E(or_2_out), .Q(mem_1_8_q));
  MEM_1 mem_1_9 (.s(mem_1_8_q), .E(or_1_out), .Q(mem_1_9_q));
  not not_7 (not_7_out, mem_1_10_q);
  MEM_1 mem_1_10 (.s(mem_1_9_q), .E(or_2_out), .Q(mem_1_10_q));
  and and_5 (step_6, mem_1_10_q, not_8_out);
  MEM_1 mem_1_11 (.s(mem_1_10_q), .E(or_1_out), .Q(mem_1_11_q));
  not not_8 (not_8_out, step_7);
  MEM_1 mem_1_12 (.s(mem_1_11_q), .E(or_2_out), .Q(step_7));

  // Notes on the sheet:
  //   reset: pull=down
endmodule

module CYCLED_STEPPER (
  input  clk,
  output step_1,
  output step_2,
  output step_3,
  output step_4,
  output step_5,
  output step_6,
  output step_7
);

  wire mem_1_1_q, mem_1_2_q, mem_1_3_q, mem_1_4_q, mem_1_5_q, mem_1_6_q, mem_1_7_q, mem_1_8_q, mem_1_9_q,
       mem_1_10_q, mem_1_11_q, not_1_out, not_2_out, not_3_out, not_4_out, not_5_out, not_6_out, not_7_out,
       not_8_out, or_1_out, or_2_out;

  not not_1 (not_1_out, clk);
  not not_2 (not_2_out, step_7);
  or or_1 (or_1_out, step_7, clk);
  or or_2 (or_2_out, step_7, not_1_out);
  or or_3 (step_1, step_7, not_3_out);
  MEM_1 mem_1_1 (.s(not_2_out), .E(or_1_out), .Q(mem_1_1_q));
  not not_3 (not_3_out, mem_1_2_q);
  MEM_1 mem_1_2 (.s(mem_1_1_q), .E(or_2_out), .Q(mem_1_2_q));
  and and_1 (step_2, mem_1_2_q, not_4_out);
  not not_4 (not_4_out, mem_1_4_q);
  MEM_1 mem_1_3 (.s(mem_1_2_q), .E(or_1_out), .Q(mem_1_3_q));
  MEM_1 mem_1_4 (.s(mem_1_3_q), .E(or_2_out), .Q(mem_1_4_q));
  and and_2 (step_3, mem_1_4_q, not_5_out);
  MEM_1 mem_1_5 (.s(mem_1_4_q), .E(or_1_out), .Q(mem_1_5_q));
  not not_5 (not_5_out, mem_1_6_q);
  MEM_1 mem_1_6 (.s(mem_1_5_q), .E(or_2_out), .Q(mem_1_6_q));
  and and_3 (step_4, mem_1_6_q, not_6_out);
  not not_6 (not_6_out, mem_1_8_q);
  MEM_1 mem_1_7 (.s(mem_1_6_q), .E(or_1_out), .Q(mem_1_7_q));
  and and_4 (step_5, mem_1_8_q, not_7_out);
  MEM_1 mem_1_8 (.s(mem_1_7_q), .E(or_2_out), .Q(mem_1_8_q));
  MEM_1 mem_1_9 (.s(mem_1_8_q), .E(or_1_out), .Q(mem_1_9_q));
  not not_7 (not_7_out, mem_1_10_q);
  MEM_1 mem_1_10 (.s(mem_1_9_q), .E(or_2_out), .Q(mem_1_10_q));
  and and_5 (step_6, mem_1_10_q, not_8_out);
  MEM_1 mem_1_11 (.s(mem_1_10_q), .E(or_1_out), .Q(mem_1_11_q));
  not not_8 (not_8_out, step_7);
  MEM_1 mem_1_12 (.s(mem_1_11_q), .E(or_2_out), .Q(step_7));
endmodule

module Active_Low_SR_Latch (
  input  s,
  input  r,
  output Q,
  output NQ
);

  nand nand_1 (Q, s, NQ);
  nand nand_2 (NQ, Q, r);
endmodule

module _2_x_4_Decoder (
  input  A,
  input  B
);

  wire _00_out, _01_out, _10_out, _11_out, not_1_out, not_2_out;

  not not_1 (not_1_out, A);
  not not_2 (not_2_out, B);
  and _00 (_00_out, not_1_out, not_2_out);
  and _01 (_01_out, not_1_out, B);
  and _10 (_10_out, A, not_2_out);
  and _11 (_11_out, A, B);

  // Notes on the sheet:
  //   !A
  //   !B
endmodule

module Active_High_SR_Latch_w__Enable (
  input  s,
  input  E,
  output Q,
  output NQ
);

  wire nand_1_out, nand_2_out, not_1_out;

  not not_1 (not_1_out, s);
  nand nand_1 (nand_1_out, s, E);
  nand nand_2 (nand_2_out, E, not_1_out);
  nand nand_3 (Q, nand_1_out, NQ);
  nand nand_4 (NQ, Q, nand_2_out);
endmodule

module register_model (
  input  [7:0] i,
  input  set,
  input  enable,
  output [7:0] o
);

  wire [7:0] mem_8_1_out_3;

  MEM_8 mem_8_1 (.\input (i), .out_3(mem_8_1_out_3), .set(set));
  CPU_ENABLE cpu_enable_1 (.\input (mem_8_1_out_3), .out_3(o), .enable(enable));

  // Notes on the sheet:
  //   simple version w/ no buffer or control
endmodule

module half_adder (
  input  a,
  input  b,
  output sum,
  output carry
);

  xor xor_1 (sum, a, b);
  and and_1 (carry, a, b);
endmodule
