// Logisim project helper_circuits.circ as structural Verilog: 5 circuits, main circuit main
module main (
  input  s,
  input  r,
  output Q,
  output NQ
);

  nand nand_1 (Q, s, NQ);
  nand nand_2 (NQ, Q, r);
endmodule

module Active_Low_SR_Latch (
  input  s,
  input  r,
  output Q,
  output NQ
);

  nand nand_1 (Q, s, NQ);
  nand nand_2 (NQ, Q, r);
endmodule

module _2_x_4_Decoder (
  input  A,
  input  B
);

  wire _00_out, _01_out, _10_out, _11_out, not_1_out, not_2_out;

  not not_1 (not_1_out, A);
  not not_2 (not_2_out, B);
  and _00 (_00_out, not_1_out, not_2_out);
  and _01 (_01_out, not_1_out, B);
  and _10 (_10_out, A, not_2_out);
  and _11 (_11_out, A, B);

  // Notes on the sheet:
  //   !A
  //   !B
endmodule

module Active_High_SR_Latch_w__Enable (
  input  s,
  input  E,
  output Q,
  output NQ
);

  wire nand_1_out, nand_2_out, not_1_out;

  not not_1 (not_1_out, s);
  nand nand_1 (nand_1_out, s, E);
  nand nand_2 (nand_2_out, E, not_1_out);
  nand nand_3 (Q, nand_1_out, NQ);
  nand nand_4 (NQ, Q, nand_2_out);
endmodule

module enable_system (
  input  [7:0] \input ,
  input  enable,
  output [7:0] out_3
);

  and and_1 (out_3[0], \input [0], enable);
  and and_2 (out_3[1], \input [1], enable);
  and and_3 (out_3[2], \input [2], enable);
  and and_4 (out_3[3], \input [3], enable);
  and and_5 (out_3[4], \input [4], enable);
  and and_6 (out_3[5], \input [5], enable);
  and and_7 (out_3[6], \input [6], enable);
  and and_8 (out_3[7], \input [7], enable);
endmodule
